# Fritzing sketch A1_4 (saved by Fritzing 0.9.3b)
perfboards: 1

parts:
  U2 = 4-Channel 5v Relay Shield [package=relay-4ch5v10a]
  Part1 = Arduino Nano (Rev3.0)
  Part2 = NRF24L01+ Breakout Board  # not connected

nets:
  VCC: U2.VCC, Part1.5V
  GND: U2.GND, Part1.GND
  N1: U2.IN1, Part1.D2
  N2: U2.IN2, Part1.D4
  N3: U2.IN4, Part1.D8
  N4: U2.IN3, Part1.D6

custom parts:
  4-Channel 5v Relay Shield: 4 Channel 5v Relay Shield w. 2x SPD-06VDC-SD-C
