# Fritzing sketch NRF24L01 [v2] (saved by Fritzing 0.9.3b)
circuit board: 6cm x 4cm
perfboards: 2

parts:
  HLK-PM1 = HLK-PM01
  U2 = SWITCH-SPST-2 [package=switch-spst-vertical]
  Radio = NRF24L01+ Breakout Board
  Power_plug1 = Power plug
  Arduino = Arduino Nano (Rev3.0)
  Cap = Capacitor [package=cap-pth-5mm]
  JP1 = Header 1 [package=1x01_offset]
  JP2 = Header 1 [package=1x01_offset]
  JP3 = Header 1 [package=1x01_offset]
  JP4 = Header 1 [package=1x01_offset]
  JP5 = Header 1 [package=1x01_offset]
  VIN7 = Header 1 [package=1x01_offset]
  VIN8 = Header 1 [package=1x01_offset]
  J1 = screw terminal, 3 pins

nets:
  N1: HLK-PM1.AC#0, U2.P
  N2: HLK-PM1.AC#1, Power_plug1.GND
  GND: HLK-PM1.-Vo, Radio.GND, Arduino.GND, Cap.2
  N3: HLK-PM1.+Vo, Arduino.5V
  N4: U2.O, Power_plug1.VCC
  VCC: Radio.VCC, Arduino.3V3, Cap.1
  N5: Radio.CE, Arduino.D9
  N6: Radio.CS, Arduino.D10
  N7: Radio.SCK, Arduino.D13/SCK
  N8: Radio.MOSI, Arduino.D11/MOSI
  N9: Radio.MISO, Arduino.D12/MISO
  N10: Arduino.D2, JP1.1
  N11: Arduino.D3, JP2.1
  N12: Arduino.D4, JP3.1
  N13: Arduino.D5, JP5.1
  N14: Arduino.D6, JP4.1
  N15: Arduino.D7, VIN7.1
  N16: Arduino.D8, VIN8.1
  N17: Arduino.VIN, J1.pin3

notes:
  Version 2
  -AC power supply
  -RJ45
  If you have a regulated 5V supply, you should just connect to the 5V pin / node.
  Vin has a regulator which supplies 5V to the 5V pin / node.
  The regulator needs >7V to properly regulate down to 5V.
  Putting 5V in will get you less than 5V out, leading to unstable operation.

// code stored in the sketch: _1_FrontDoor.ino

#define SN "Front Door"                 // short Sketch name
#define SV "0.9"                        // short Sketch version
#define MY_NODE_ID 1                    // (1-254) to manually set Node ID

/* Includes
=========1=========2=========3=========4=========5=========6=========7========*/
#include "NRF24L01.h"                   // NRF24L01 definitions
#include <MySensors.h>                  // MySensors library
#include "zzz.h"                        // Explanation and inital variables

//#include "a0.h"                         // Relay, to switch on the lights when needed
//#include "a1.h"                         // Lock and unlock the front door

#include "s0.h"                         // PIR switch, check if someone is in front of the door
#include "s1.h"                         // Reed switch, check if door is open or closed
#include "s2.h"                         // Photovoltaic sensor, to check if it's dark

/* Presentation
=========1=========2=========3=========4=========5=========6=========7========*/
void presentation(){ 
    sendSketchInfo(SN, SV);             // Send the sketch version information
    // Register the sensor(s) to the controller
    /* void present(uint8_t childSensorId, uint8_t sensorType, const char *description, bool ack); */
    present(0, S_MOTION, "PIR switch");
    present(1, S_DOOR, "Reed switch");
    present(2, S_LIGHT_LEVEL, "PV switch");
//    present(3, S_BINARY, "Lights relay");
    //Serial.println("=== Node presented === ");
}

/* Setup
=========1=========2=========3=========4=========5=========6=========7========*/
void setup() {
    setup_s0();
    setup_s1();
    setup_s2();
//    setup_a0();
    //Serial.println( "=== Node setup done ===" );
}

/* Loop
=========1=========2=========3=========4=========5=========6=========7========*/
void loop() {
    loop_s0();
    loop_s1();
    loop_s2();
    wait(2000);                         // wait a bit, loop once every 2 seconds
}

/* Receive
=========1=========2=========3=========4=========5=========6=========7========*/
/*void receive(const MyMessage &message) {
//    receive_a0(message);
    //Serial.println("=== Node message received === ");
}*/

// code stored in the sketch: _3_Patio.ino
#define SN "Patio"                      // short Sketch (Node) name
#define SV "1.1"                        // short Sketch (Node) version
#define MY_NODE_ID 1                    // (1-254) to manually set Node ID

/* Includes
=========1=========2=========3=========4=========5=========6=========7========*/
#include "NRF24L01.h"                   // NRF24L01 definitions
#include <MySensors.h>                  // MySensors library
#include "s1.h"                         // DHT11 for Temperature and Humidity
#include "a1.h"                         // Relay for Spotlight

/* Presentation
=========1=========2=========3=========4=========5=========6=========7========*/
void presentation(){ 
    sendSketchInfo(SN, SV);             // Send the sketch version information
    // Register sensor(s) to gateway    // void present(uint8_t childSensorId, uint8_t sensorType, const char *description, bool ack);
    present(0, S_HUM,"Patio Humidity");             // present sensor to gateway
    present(1, S_TEMP,"Patio Temperature");         // present sensor to gateway
    present(2, S_BINARY,"Patio Spotlight");         // present sensor to gateway
    metric = getConfig().isMetric;                  // ???
    //Serial.println("=== Node presented === ");    // Debug
}

/* Setup
=========1=========2=========3=========4=========5=========6=========7========*/
void setup(){
    setup_a1();
    setup_s1();
    //Serial.println( "=== Node setup done ===" ); // Debug
}

/* Loop
=========1=========2=========3=========4=========5=========6=========7========*/
void loop(){
    loop_s1();
}

/* Receive
=========1=========2=========3=========4=========5=========6=========7========*/
void receive(const MyMessage &message) {
    receive_a1(message);
    //Serial.println("=== Node message received === "); // Debug
}

// code stored in the sketch: a0.h
/*
    Single Relay actuator for door lights

=========1=========2=========3=========4=========5=========6=========7========*/
MyMessage msg_a0(3, V_STATUS);          // define type of message sent to MySensors

/* Setup
=========1=========2=========3=========4=========5=========6=========7========*/
void setup_a0(){
    pinMode(relayPin, OUTPUT);         // set pin to output mode
}

/* Receive
=========1=========2=========3=========4=========5=========6=========7========*/
void receive_a0(const MyMessage &message){
    if (message.type==V_LIGHT) {       // We only expect one type of message from controller.
        digitalWrite(relayPin, message.getBool() ? 1 : 0);  // Toggle relay state
        // Serial.print("Toggle relay. New state is "); Serial.println(message.getBool());
   } 
}

/* ON
=========1=========2=========3=========4=========5=========6=========7========*/
void lightsOn(){
    if (pvState < 500) {               // only switch on if PV sensor says it's dark
        digitalWrite(relayPin, 1);     // switch off 
    }
}

/* OFF
=========1=========2=========3=========4=========5=========6=========7========*/
void lightsOff(int t){
    wait(t * 60 * 1000);               // wait for t minutes
    digitalWrite(relayPin, 0);         // then switch off 
}

// code stored in the sketch: a0.h.ino
/* Single Relay actuator
=========1=========2=========3=========4=========5=========6=========7========*/
const int relayPin = 3;                 // define switch pin
MyMessage msgRel(3, V_STATUS);          // define type of message sent to MySensors

/* Setup
=========1=========2=========3=========4=========5=========6=========7========*/
void setup_s3(){
    pinMode(3, OUTPUT);                     // set pin 3 in output mode
    /*digitalWrite(relayPin, loadState(3) ? 1 : 0);  // Set relay to last known state (using eeprom storage) */
}

/* Receive
=========1=========2=========3=========4=========5=========6=========7========*/
void receive_s3(const MyMessage &message){
    if (message.type==V_LIGHT) {                           // We only expect one type of message from controller.
        digitalWrite(relayPin, message.getBool() ? 1 : 0);  // Toggle relay state
        /*saveState(3, message.getBool());                // Store state in eeprom*/
        // Serial.print("Toggle relay. New state is "); Serial.println(message.getBool());
   } 
}

// code stored in the sketch: a1.h
/* Single Relay actuator
=========1=========2=========3=========4=========5=========6=========7========*/
MyMessage msgRel(2, V_LIGHT);
#define relayPin  3                     // Digital pin number for the relay
#define RELAY_ON 1                      // GPIO value to write to turn on attached relay
#define RELAY_OFF 0                     // GPIO value to write to turn off attached relay

/* Setup
=========1=========2=========3=========4=========5=========6=========7========*/
void setup_a1(){
    pinMode(relayPin, OUTPUT);                              // set relay pin in output mode
    digitalWrite(3, loadState(3) ? RELAY_ON : RELAY_OFF);   // Set relay to last known state (using eeprom storage) 
}

/* Receive
=========1=========2=========3=========4=========5=========6=========7========*/
void receive_a1(const MyMessage &message){
    // We only expect one type of message from controller. But we better check anyway.
    if (message.type==V_LIGHT) {
        // Change relay state
        digitalWrite(3, message.getBool() ? RELAY_ON : RELAY_OFF);
        // Store state in eeprom
        saveState(3, message.getBool());
        // Write some debug info
        Serial.print("Incoming change for relay:"); Serial.print(3);
        Serial.print(", New state: "); Serial.println(message.getBool());
   } 
}

// code stored in the sketch: s0.h
/* 
    Passive InfraRed Switch

=========1=========2=========3=========4=========5=========6=========7========*/
MyMessage msg_s0(0, V_TRIPPED);        // define type of message sent to MySensors

/* Setup
=========1=========2=========3=========4=========5=========6=========7========*/
void setup_s0(){
    pinMode(pirPin, INPUT);            // initialize sensor as an input
}

/* Loop
=========1=========2=========3=========4=========5=========6=========7========*/
void loop_s0(){
    pirVal = digitalRead(pirPin);               // read and store sensor value
    //Serial.print("PIR is at: "); Serial.println(pirVal);
    if (pirVal == HIGH && pirState == LOW) {    // check if the sensor is tripped
        Serial.println("-----> Motion detected!");
        pirState = HIGH;       	                // update variable state to HIGH
        pirTimer ++;
//        lightsOn();                           // Switch on lights
    }
    if (pirState == HIGH && pirTimer>60){
        pirState = LOW;                           // update variable state to LOW
        pirTimer=0;
//        lightsOff(5);                         // Set timer to switch off light 5 minutes
    }
    send(msg_s0.set(pirVal ? "1" : "0"));       // Send tripped value to gw
}

// code stored in the sketch: s1.h
/*
    Reed Switch

=========1=========2=========3=========4=========5=========6=========7========*/
MyMessage msg_s1(1, V_TRIPPED);        // define type of message sent to MySensors

/* Setup
=========1=========2=========3=========4=========5=========6=========7========*/
void setup_s1(){
    pinMode(reedPin, INPUT);           // initialize sensor as an input
}

/* Loop
=========1=========2=========3=========4=========5=========6=========7========*/
void loop_s1(){
    reedVal = digitalRead(reedPin);   	 // read and store sensor value
    //Serial.print("Reed is at: "); Serial.println(reedVal);
    if (reedVal == HIGH) {        // check if the sensor is tripped
        Serial.println("Your Door is Closed");
    } else {
        Serial.println("Your Door is Open");
    }
    send(msg_s1.set(reedVal ? "0" : "1"));       // Send tripped value to gw
}

// code stored in the sketch: s2.h
/*
    PhotoVoltaic Sensor

=========1=========2=========3=========4=========5=========6=========7========*/
MyMessage msg_s2(2, V_LIGHT_LEVEL);    // define type of message sent to MySensors

/* Setup
=========1=========2=========3=========4=========5=========6=========7========*/
void setup_s2(){
    pinMode(pvPin, INPUT);             // initialize sensor as an input
}

/* Loop
=========1=========2=========3=========4=========5=========6=========7========*/
void loop_s2(){
    pvVal = analogRead(pvPin);   	   // read and store sensor value
    Serial.print("Light is at: "); Serial.println(pvVal);
    if (pvState != pvVal){             // if the state has changed
        pvState = pvVal;               // update state
        //  send message to mycontroller
        send(msg_s2.set(pvVal));
    }
}

/*
    // a few threshholds, qualitatively determined
    if (pvVal < 10) {
        Serial.println(" - Dark");
    } else if (pvVal < 200) {
        Serial.println(" - Dim");
    } else if (pvVal < 500) {
        Serial.println(" - Light");
    } else if (pvVal < 800) {
        Serial.println(" - Bright");
    } else {
        Serial.println(" - Very bright");
    }
 */

// code stored in the sketch: s3.h
/* Single Relay actuator
=========1=========2=========3=========4=========5=========6=========7========*/
const int relayPin = 3;                 // define switch pin
MyMessage msgRel(3, V_STATUS);          // define type of message sent to MySensors

/* Setup
=========1=========2=========3=========4=========5=========6=========7========*/
void setup_s3(){
    pinMode(3, OUTPUT);                     // set pin 3 in output mode
    /*digitalWrite(relayPin, loadState(3) ? 1 : 0);  // Set relay to last known state (using eeprom storage) */
}

/* Receive
=========1=========2=========3=========4=========5=========6=========7========*/
void receive_s3(const MyMessage &message){
    if (message.type==V_LIGHT) {                           // We only expect one type of message from controller.
        digitalWrite(relayPin, message.getBool() ? 1 : 0);  // Toggle relay state
        /*saveState(3, message.getBool());                // Store state in eeprom*/
        // Serial.print("Toggle relay. New state is "); Serial.println(message.getBool());
   } 
}

// code stored in the sketch: xxx.h
/*
    FRONT DOOR

    RADIO
repeater

    SENSORS
PIR switch - to check if someone is in front of the door
Reed switch - to sense if door is open or closed
Photovoltaic sensor -  to check if it's day or night
? Electric lock - status if door is locked

    ACTUATORS
Relay, to switch on the lights
? Lock/Unlock via electrick lock

*/

// code stored in the sketch: zzz.h
/*  
				FRONT DOOR
*/
//
//  SENSORS
//
/*=======1=========2=========3=========4=========5=========6=========7========*/
//
//  s0    PIR switch - to check if someone is in front of the door
//
const int pirPin = 2;                  // the pin that the PIR motion detector is atteched to
int pirState = LOW;                    // by default, no motion is detected
int pirVal = 0;                        // variable to store the PIR value
int pirTimer =0;                       // variable to store the number of loops
//
//  s1  Reed switch - to sense if the door is open or closed
//
const int reedPin = 3;                 // the pin that the reed switch is atteched to
int reedVal = 0;                       // variable to store the reed switch last state
//
//  s2  Photovoltaic sensor -  to check if it's day or night
//
const int pvPin = A0;                  // the pin that the photovoltaic sensor is attached to
int pvState = 0;                       // default state, dark
int pvVal = 0;                         // variable to store photovoltaic sensor value
//
//  ACTUATORS
//
/*=======1=========2=========3=========4=========5=========6=========7========*/
//
//  a0  Relay, to switch on the lights if it's dark and motion is detected
//
const int relayPin = 5;                 // the pin that the relay is atteched to
int relayState = 0;                     // by default, the relay is off
//
//  a1 Lock/Unlock via electrick lock  ???
//
const int lockPin = 6;                  // the pin that the door relay is atteched to
int lockState = 0;                      // by default, the door is locked
