# Fritzing sketch PIR (saved by Fritzing 0.9.3b)
perfboards: 1

parts:
  Part3 = Arduino Nano (Rev3.0)
  Part4 = NRF24L01+ Breakout Board  # not connected
  PIR2 = PIR sensor

nets:
  GND: Part3.GND, PIR2.GND
  5V: Part3.5V, PIR2.VDD
  N1: Part3.A2, PIR2.SIG
