# Fritzing sketch Untitled Sketch (saved by Fritzing 0.9.3b)
circuit board: 4cm x 5cm
perfboards: 1

parts:
  JP2 = Header 8 [package=1x08_smd]
  Part2 = NRF24L01+ Breakout Board
  HLK-PM1 = HLK-PM01
  JP1 = Header 8 [package=1x08_smd]
  Part1 = Arduino Nano (Rev3.0)

nets:
  N1: JP2.1, Part1.A0
  N2: JP2.2, Part1.A1
  N3: JP2.3, Part1.A2
  N4: JP2.4, Part1.A3
  N5: JP2.5, Part1.A4
  N6: JP2.6, Part1.A5
  N7: JP2.7, Part1.A6
  N8: JP2.8, Part1.A7
  GND: Part2.GND, HLK-PM1.-Vo, Part1.GND
  VCC: Part2.VCC, Part1.3V3
  N9: Part2.CE, JP1.1, Part1.D9
  N10: Part2.CS, Part1.D10
  N11: Part2.SCK, Part1.D13/SCK
  N12: Part2.MOSI, Part1.D11/MOSI
  N13: Part2.MISO, Part1.D12/MISO
  N14: HLK-PM1.+Vo, Part1.5V
  N15: JP1.2, Part1.D8
  N16: JP1.3, Part1.D7
  N17: JP1.4, Part1.D6
  N18: JP1.5, Part1.D5
  N19: JP1.6, Part1.D4
  N20: JP1.7, Part1.D3
  N21: JP1.8, Part1.D2
