# Fritzing sketch node00_Office (saved by Fritzing 0.9.3b)

parts:
  Part1 = Arduino Uno (Rev3)  # not connected
  Part2 = Arduino Ethernet Shield (Rev3)
  Part3 = NRF24L01+ Breakout Board [part_number=GW]
  KY-1 = Keyes Relay [part_number=A1 package=THT]
  S2 = Reed switch [part_number=S1 package=THT]
  DHT1 = DHT11 Humitidy and Temperature Sensor

nets:
  GND: Part2.GND, Part3.GND, KY-1.ground, S2.pin_1, DHT1.GND
  N1: Part2.A0, Part3.SCK
  N2: Part2.A1, Part3.MOSI
  N3: Part2.A2, Part3.MISO
  N4: Part2.D2, KY-1.signal
  N5: Part2.PWM_D3, DHT1.DATA
  N6: Part2.SDCS, S2.pin_2
  N7: Part2.PWM_D5, Part3.CE
  N8: Part2.PWM_D6, Part3.CS
  3V3: Part2.3V3, Part3.VCC
  5V: Part2.5V, KY-1.power, DHT1.VDD

custom parts:
  Keyes Relay: The Keyes 5V relay module is suitable for SCM development, home appliance control. It uses a 5V~12V TIL control signal which can control DC / AC signal.
  DHT11 Humitidy and Temperature Sensor: DHT11 Humidity and Temperature Sensor

// code stored in the sketch: _0_OfficeGateway.ino

#define SN "Gateway"                    // short Sketch (Node) name
#define SV "1.1"                        // short Sketch (Node) version
//#define MY_NODE_ID 0                  // (1-254) to manually set Node ID

/* Includes
=========1=========2=========3=========4=========5=========6=========7========*/
#include "RadioGateway.h"               // NRF24L01 definitions
#include <Ethernet.h>                   // Ethernet library for W5100 shield
#include <MySensors.h>                  // MySensors library
#include "zzz.h"                        // Explanation and inital variables

#include "s0.h"                         // Hall switch
#include "s1.h"                         // PV sensor

#include "a0.h"                         // Relay for BBQ reflector
#include "a1.h"                         // Relay for projector cord

/* Presentation
=========1=========2=========3=========4=========5=========6=========7========*/
void presentation(){ 
    sendSketchInfo(SN, SV);             // Send the sketch version information
    // Register the sensor(s) to the controller
    /* void present(uint8_t childSensorId, uint8_t sensorType, const char *description, bool ack); */
    present(0, S_LIGHT, "BBQ Reflector");
    present(1, S_LIGHT, "Projector cord");
    present(2, S_LOCK, "Office Door");
    present(3, S_LIGHT_LEVEL, "PV Sensor");
    //Serial.println("=== Gateway presented === ");
}
/* Setup
=========1=========2=========3=========4=========5=========6=========7========*/
void setup(){
    setup_a0();
    setup_a1();
    setup_s0();
    setup_s1();
    //Serial.println( "=== Gateway setup done ===" );
}

/* Loop
=========1=========2=========3=========4=========5=========6=========7========*/
void  loop(){
    loop_s0();
    loop_s1();
    wait(1000);                         // wait a bit, loop once per second
}

/* Receive
=========1=========2=========3=========4=========5=========6=========7========*/
void receive(const MyMessage &message) {
    receive_a0(message);
    receive_a1(message);
    //Serial.println("=== Node message received === ");
}

// code stored in the sketch: a0.h
/* Relay for BBQ reflector light
=========1=========2=========3=========4=========5=========6=========7========*/
MyMessage msg_a0(0, V_STATUS);          // define type of message sent to MySensors

/* Setup
=========1=========2=========3=========4=========5=========6=========7========*/
void setup_a0(){
    pinMode(bbqPin, OUTPUT);           // define switch as an input port
}

/* Receive
=========1=========2=========3=========4=========5=========6=========7========*/
void receive_a0(const MyMessage &message){
    if (message.type==V_LIGHT) {       // We only expect one type of message from controller.
        digitalWrite(bbqPin, message.getBool() ? 1 : 0);  // Toggle relay state
        // Serial.print("Toggle relay. New state is "); Serial.println(message.getBool());
   }
}

// code stored in the sketch: A1.h
/*
    Single Relay
*/

/* Initialize
=========1=========2=========3=========4=========5=========6=========7========*/
MyMessage msgA1(A1, V_STATUS);


/* Setup
=========1=========2=========3=========4=========5=========6=========7========*/
void setupA1(){
	// set relay pin in output mode
    pinMode(pinA1, OUTPUT);
	// load state from eeprom
	digitalWrite(pinA1, loadState(A1));
}


/* Receive
=========1=========2=========3=========4=========5=========6=========7========*/
void receiveA1(const MyMessage &message){
    if (message.type==V_STATUS) {
		// toggle relay state
		digitalWrite(pinA1,message.getBool());
		// save state to eeprom
		saveState(A1,message.getBool());
		// Printout
		Serial.println((String)"Toggle A1 relay. New state is "+message.getBool());
	}
}

// code stored in the sketch: def.h

/*  SENSOR IDs
=========1=========2=========3=========4=========5=========6=========7========*/
#define A1              1               // Relay
#define S1              2               // Reed switch
#define S2T             3               // Temperature
#define S2H             4               // Humidity


/*  PINS & VARIABLES
=========1=========2=========3=========4=========5=========6=========7========*/

// A1 - Relay for projector power cord
// -----------------------------------
const int pinA1 =       2;              // the pin that the relay is atteched to

// S1 - Reed switch - office door
// ------------------------------
const int pinS1 =       4;              // data pin with pull-up resistor
int valueS1 = 0;                        // reading the sensor status
int stateS1 = 0;                        // storing the last state

// S2 - Temperature & Humidity (DHT 11)
// ------------------------------------
const int pinS2 =       3;              // The pin for DHT data 
float stateS2H;                         // last saved humidity value
float stateS2T;                         // last saved temperature value
unsigned long tS2 = 0;                  // last saved time the loop fired
unsigned long iS2 = 5;                  // interval at which to fire loop (in minutes)

// code stored in the sketch: GW.h
/* NRF24L01 defintions
=========1=========2=========3=========4=========5=========6=========7========*/
//#define MY_DEBUG                               // Enable debug prints to serial monitor
//#define MY_DEBUG_VERBOSE_RF24                  // Enable for verbose debug prints related to the RF24 driver. Requires DEBUG to be enabled.

#define MY_RADIO_NRF24                           // Enable and select radio type attached
#define MY_RF24_PA_LEVEL RF24_PA_MAX             // Set radio power
#define MY_RF24_DATARATE RF24_250KBPS            // Set radio transmission rate

/* MQTT definitions
=========1=========2=========3=========4=========5=========6=========7========*/
#define MY_GATEWAY_MQTT_CLIENT                   // MQTT client
#define MY_MQTT_PUBLISH_TOPIC_PREFIX "AD_gw_out"
#define MY_MQTT_SUBSCRIBE_TOPIC_PREFIX "AD_gw_in"
#define MY_MQTT_CLIENT_ID "AD_gateway"           // Set MQTT client id

/* w5100 setup
=========1=========2=========3=========4=========5=========6=========7========*/
//#define MY_W5100_SPI_EN 4                      // W5100 Ethernet module SPI enable (keep disabled)
#if !defined(MY_W5100_SPI_EN) && !defined(ARDUINO_ARCH_SAMD)
  #define MY_SOFTSPI                             // Enable Soft SPI for NRF radio (note different radio wiring is required)
  #define MY_SOFT_SPI_SCK_PIN 14                 // (A0)
  #define MY_SOFT_SPI_MOSI_PIN 15                // (A1)
  #define MY_SOFT_SPI_MISO_PIN 16                // (A2)
#endif  
#define MY_RF24_CE_PIN 5                         // For W5100 we have to move CE pin for radio
#define MY_RF24_CS_PIN 6                         // For W5100 we have to move CSN pin for radio

/* MQTT broker definitions
=========1=========2=========3=========4=========5=========6=========7========*/
//#define MY_MQTT_USER "yypgbgnf"
//#define MY_MQTT_PASSWORD "gelw1BJpmddw"
//#define MY_CONTROLLER_IP_ADDRESS 54,196,24,81
//#define MY_PORT 15089

#define MY_MQTT_USER "AD"
#define MY_MQTT_PASSWORD "AD"
#define MY_CONTROLLER_IP_ADDRESS 10,0,0,32
#define MY_PORT 1883


/* IP Address (or DHCP)
=========1=========2=========3=========4=========5=========6=========7========*/
#define MY_IP_ADDRESS 10,0,0,33                   // Enable MY_IP_ADDRESS here if you want a static ip address (no DHCP)
#define MY_IP_GATEWAY_ADDRESS 10,0,0,1            // If using static ip you need to define Gateway and Subnet address as well
#define MY_IP_SUBNET_ADDRESS 255,255,255,0        // When this doesnt work, check what pins are being used!!!

/* Optional & Additional
=========1=========2=========3=========4=========5=========6=========7========*/
//#define MY_RF24_CHANNEL 76                    // Change radio channel, has to be done on all nodes

//#define MY_SIGNING_ATSHA204                   // Enables hardware signing using ATSHA204
//#define MY_SIGNING_SOFT                       // Enables software signing

//#define MY_PARENT_NODE_ID                             
//#define MY_PARENT_NODE_IS_STATIC

//#define MY_DISABLED_SERIAL                    // Enable if you want to use TX(1), RX(0) as normal I/O pin
//#define MY_RF24_ENABLE_ENCRYPTION

// code stored in the sketch: node00_Office.ino
#define SN "Gateway"                    // short Sketch (Node) name
#define SV "1.1"                        // short Sketch (Node) version
#define MY_NODE_ID 00                   // (1-254) to manually set Node ID
/*
    Includes
=========1=========2=========3=========4=========5=========6=========7========*/
#include <SPI.h>                        // Serial Peripheral Interface Bus
#include <Ethernet.h>                   // Ethernet library for W5100 shield
#include "GW.h"                         // NRF24L01 definitions for Gateway
#include <MySensors.h>                  // MySensors library
#include "def.h"                        // Explanations and initialization
  #include "A1inverted.h"               // Projector power cord (Relay Switch)
  #include "S1.h"                       // Office Door (Reed switch)
  #include "S2.h"                       // DHT 11 for Humidity and Temperature
/*
    Presentation
=========1=========2=========3=========4=========5=========6=========7========*/
void presentation(){ 
  sendSketchInfo(SN, SV);
    present(A1, S_BINARY, "Projector Power");
    present(S1, S_DOOR, "Office Door Reed");
    present(S2T, S_TEMP,"Office Temperature");
    present(S2H, S_HUM,"Office Humidity");
  Serial.println((String)"\n === Node "+MY_NODE_ID+" presented ("+SN+")\n");
}
/*
    Setup
=========1=========2=========3=========4=========5=========6=========7========*/
void setup(){
    setupA1();
    setupS1();
    setupS2();
  Serial.println((String)"\n === Node "+MY_NODE_ID+" setup ("+SN+")\n");
}
/*
    Loop
=========1=========2=========3=========4=========5=========6=========7========*/
void loop(){
    loopS1();
    loopS2();
  wait(1000);
}
/*
    Receive
=========1=========2=========3=========4=========5=========6=========7========*/
void receive(const MyMessage &message) {
    receiveA1(message);
}

// code stored in the sketch: RadioGateway.h
/* NRF24L01 defintions
=========1=========2=========3=========4=========5=========6=========7========*/
#define MY_DEBUG                                    // Enable debug prints to serial monitor
#define MY_RADIO_NRF24                              // Enable and select radio type attached
#define MY_RF24_PA_LEVEL RF24_PA_MAX                // Set radio power
#define MY_RF24_DATARATE RF24_250KBPS               // Set radio transmission rate

/* MQTT defintions
=========1=========2=========3=========4=========5=========6=========7========*/
//#define MY_MQTT_USER "yypgbgnf"
//#define MY_MQTT_PASSWORD "gelw1BJpmddw"
//#define MY_CONTROLLER_IP_ADDRESS 54,196,24,81
//#define MY_PORT 15089
#define MY_MQTT_USER ""
#define MY_MQTT_PASSWORD ""
#define MY_CONTROLLER_IP_ADDRESS 10,0,0,32
#define MY_PORT 1883

#define MY_GATEWAY_MQTT_CLIENT                      // MQTT client
#define MY_MQTT_CLIENT_ID "ADgw"                    // Set MQTT client id
#define MY_MQTT_PUBLISH_TOPIC_PREFIX "gw-out"
#define MY_MQTT_SUBSCRIBE_TOPIC_PREFIX "gw-in"

/* w5100 setup
=========1=========2=========3=========4=========5=========6=========7========*/
#define MY_W5100_SPI_EN 4                           // W5100 Ethernet module SPI enable
#define MY_RF24_CE_PIN 5                            // For W5100 we have to move CE pin for radio
#define MY_RF24_CS_PIN 6                            // For W5100 we have to move CSN pin for radio

/* IP Address (or DHCP)
=========1=========2=========3=========4=========5=========6=========7========*/
//#define MY_IP_ADDRESS 10,0,0,33                   // Enable MY_IP_ADDRESS here if you want a static ip address (no DHCP)
//#define MY_IP_GATEWAY_ADDRESS 10,0,0,1            // If using static ip you need to define Gateway and Subnet address as well
//#define MY_IP_SUBNET_ADDRESS 255,255,255,0

/* Optional & Additional
=========1=========2=========3=========4=========5=========6=========7========*/
//#define MY_RF24_CHANNEL 76                    // Change radio channel, has to be done on all nodes

//#define MY_SIGNING_ATSHA204                   // Enables hardware signing using ATSHA204
//#define MY_SIGNING_SOFT                       // Enables software signing

//#define MY_PARENT_NODE_ID                             
//#define MY_PARENT_NODE_IS_STATIC

//#define MY_DISABLED_SERIAL                    // Enable if you want to use TX(1), RX(0) as normal I/O pin
//#define MY_RF24_ENABLE_ENCRYPTION

// code stored in the sketch: s0.h
/* Hall Switch
=========1=========2=========3=========4=========5=========6=========7========*/
MyMessage doorMsg(2, V_TRIPPED);        // define type of message sent to MySensors

/* Setup
=========1=========2=========3=========4=========5=========6=========7========*/
void setup_s0(){
    pinMode(hallPin, INPUT);            // define input pin for reading
}

/* Loop
=========1=========2=========3=========4=========5=========6=========7========*/
void loop_s0() {
    // read the state of the hall sensor
    hallCurrentState = digitalRead(hallPin);
    
    // only do something if current state is different from previous state
    if (hallCurrentState == HIGH && hallPreviousState == 0) {
        hallPreviousState = 1;
        send(doorMsg.set(1));
        //Serial.println(" == DOOR IS OPEN == ");
    } else if (hallCurrentState == LOW && hallPreviousState == 1) {
        hallPreviousState = 0;
        send(doorMsg.set(0));
        //Serial.println(" == DOOR IS CLOSED == ");
    }
}

// code stored in the sketch: S1.h
/* 
    Reed Switch

 - 	Since one end of the reed switch is connected to ground, 
	we need to pull-up the reed switch pin internally
 - 	Use Arduino’s internal pull-up resistor to bias the switch high
 - 	This effectively inverts the behavior of the INPUT mode, 
	where HIGH means the sensor is off, and LOW means the sensor is on.

*/

/*
    Initialize
=========1=========2=========3=========4=========5=========6=========7========*/
MyMessage msgS1(S1, V_TRIPPED);         // type of message sent to MySensors
/*
    Setup
=========1=========2=========3=========4=========5=========6=========7========*/
void setupS1(){
    pinMode(pinS1, INPUT_PULLUP);       // pull-up the pin internally !!!
}
/* 
    Loop
=========1=========2=========3=========4=========5=========6=========7========*/
void loopS1(){
    valueS1 = digitalRead(pinS1);       // Read the state of the switch
    if (valueS1 != stateS1) {           // If different from last state
        if (valueS1 == LOW){            // Pin reads low, the switch is closed
            Serial.println("S1 is Closed (Door Closed/Untripped)");
        } else {
            Serial.println("S1 is Open (Door Open/Tripped)");
        }
        send(msgS1.set(valueS1));       // send to controller
        stateS1 = valueS1;              // update state
    }
}
/*
    Receive
=========1=========2=========3=========4=========5=========6=========7========*/
// nothing to receive

// code stored in the sketch: zzz.h

/*  ACTUATORS
=========1=========2=========3=========4=========5=========6=========7========*/

// Projector power cord (Relay Switch)
#define A1 1                            // Sensor number
const int pinA1 = 2;                    // data pin
                                        // power pin
                                        // ground pin

/*  SENSORS 
=========1=========2=========3=========4=========5=========6=========7========*/

//  Reed switches
#define S1 2                            // Sensor number
#define S2 3                            // Sensor number
//  Office doors, check if open
const int pinS1 = 12;                   // define switch pin
int newStateS1 = 0;                     // variable for reading the sensor status
int oldStateS1 = 0;                     // variable for storing the last state

const int pinS1 = 13;                   // define switch pin
int newStateS2 = 0;                     // variable for reading the sensor status
int oldStateS2 = 0;                     // variable for storing the last state

                                        // ground pin
