# Fritzing sketch node02_BbqArea (saved by Fritzing 0.9.3b)
circuit board: 5cm x 5cm
perfboards: 1

parts:
  S08 = SI1145 Digital UV Index + IR + Visible Light Sensor [part_number=S8]  # not connected
  S03 = Adafruit BMP180 [part_number=S3]  # not connected
  S07 = TEMPERATURE-SENSOR [part_number=S7 package=to-92]  # not connected
  A03 = Grove Infrared Emitter [part_number=A3]  # not connected
  J3 = female pin header, 11 pins [form="♀ (female)"]
  J4 = female pin header, 9 pins [form="♀ (female)"]
  NRF25 = NRF24L01+ Breakout Board [part_number=nrf]
  GND2 = female pin header, 6 pins [form="♀ (female)"]
  GND3 = female pin header, 6 pins [form="♀ (female)"]
  5_0v1 = female pin header, 6 pins [form="♀ (female)"]
  3_3v1 = female pin header, 7 pins [form="♀ (female)"]
  Arduino_Nano1 = Arduino Nano (Rev3.0)
  C3 = Capacitor Polarized [package=cpol-radial-10uf-25v]
  A01 = Keyes Relay [package=THT]  # not connected

nets:
  N1: J3.pin1, Arduino_Nano1.D1/TX
  N2: J3.pin2, Arduino_Nano1.D0/RX
  N3: J3.pin3, Arduino_Nano1.RESET
  GND: J3.pin4, NRF25.GND, GND3.pin1, GND3.pin2, GND3.pin3, GND3.pin4, GND3.pin5, GND3.pin6, Arduino_Nano1.GND, C3.-
  N4: J3.pin5, Arduino_Nano1.D2
  N5: J3.pin6, Arduino_Nano1.D3
  N6: J3.pin7, Arduino_Nano1.D4
  N7: J3.pin8, Arduino_Nano1.D5
  N8: J3.pin9, Arduino_Nano1.D6
  N9: J3.pin10, Arduino_Nano1.D7
  N10: J3.pin11, Arduino_Nano1.D8
  N11: J4.pin1, Arduino_Nano1.A7
  N12: J4.pin2, Arduino_Nano1.A6
  N13: J4.pin3, Arduino_Nano1.A5
  N14: J4.pin4, Arduino_Nano1.A4
  N15: J4.pin5, Arduino_Nano1.A3
  N16: J4.pin6, Arduino_Nano1.A2
  N17: J4.pin7, Arduino_Nano1.A1
  N18: J4.pin8, Arduino_Nano1.A0
  N19: J4.pin9, Arduino_Nano1.AREF
  VCC: NRF25.VCC, 3_3v1.pin1, 3_3v1.pin2, 3_3v1.pin3, 3_3v1.pin4, 3_3v1.pin5, 3_3v1.pin6, 3_3v1.pin7, Arduino_Nano1.3V3, C3.+
  N20: NRF25.CE, Arduino_Nano1.D9
  N21: NRF25.CS, Arduino_Nano1.D10
  N22: NRF25.SCK, Arduino_Nano1.D13/SCK
  N23: NRF25.MOSI, Arduino_Nano1.D11/MOSI
  N24: NRF25.MISO, Arduino_Nano1.D12/MISO
  N25: GND2.pin1, GND2.pin2, GND2.pin3, GND2.pin4, GND2.pin5, GND2.pin6
  N26: 5_0v1.pin1, 5_0v1.pin2, 5_0v1.pin3, 5_0v1.pin4, 5_0v1.pin5, 5_0v1.pin6, Arduino_Nano1.5V

notes:
  node 02 - BBQ

custom parts:
  SI1145 Digital UV Index + IR + Visible Light Sensor: The SI1145 is a new sensor from SiLabs with a calibrated light sensing algorithm that can calculate UV Index. It doesn't contain an actual UV sensing element, instead it approximates it based on visible & IR light from the sun. We took this outside a couple days and compared the calculated UV index with the news-reported index and found it was very accurate! It's a digital sensor that works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
  Adafruit BMP180: This precision sensor from Bosch is the best low-cost sensing solution for measuring barometric pressure and temperature. Because pressure changes with altitude you can also use it as an altimeter! The sensor is soldered onto a PCB with a 3.3V regulator, I2C level shifter and pull-up resistors on the I2C pins. The BMP180 is the next-generation of sensors from Bosch, and replaces the BMP085.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
  Keyes Relay: The Keyes 5V relay module is suitable for SCM development, home appliance control. It uses a 5V~12V TIL control signal which can control DC / AC signal.

// code stored in the sketch: _1_FrontDoor.ino

#define SN "Front Door"                 // short Sketch name
#define SV "0.9"                        // short Sketch version
#define MY_NODE_ID 1                    // (1-254) to manually set Node ID

/* Includes
=========1=========2=========3=========4=========5=========6=========7========*/
#include "NRF24L01.h"                   // NRF24L01 definitions
#include <MySensors.h>                  // MySensors library
#include "zzz.h"                        // Explanation and inital variables

//#include "a0.h"                         // Relay, to switch on the lights when needed
//#include "a1.h"                         // Lock and unlock the front door

#include "s0.h"                         // PIR switch, check if someone is in front of the door
#include "s1.h"                         // Reed switch, check if door is open or closed
#include "s2.h"                         // Photovoltaic sensor, to check if it's dark

/* Presentation
=========1=========2=========3=========4=========5=========6=========7========*/
void presentation(){ 
    sendSketchInfo(SN, SV);             // Send the sketch version information
    // Register the sensor(s) to the controller
    /* void present(uint8_t childSensorId, uint8_t sensorType, const char *description, bool ack); */
    present(0, S_MOTION, "PIR switch");
    present(1, S_DOOR, "Reed switch");
    present(2, S_LIGHT_LEVEL, "PV switch");
//    present(3, S_BINARY, "Lights relay");
    //Serial.println("=== Node presented === ");
}

/* Setup
=========1=========2=========3=========4=========5=========6=========7========*/
void setup() {
    setup_s0();
    setup_s1();
    setup_s2();
//    setup_a0();
    //Serial.println( "=== Node setup done ===" );
}

/* Loop
=========1=========2=========3=========4=========5=========6=========7========*/
void loop() {
    loop_s0();
    loop_s1();
    loop_s2();
    wait(2000);                         // wait a bit, loop once every 2 seconds
}

/* Receive
=========1=========2=========3=========4=========5=========6=========7========*/
/*void receive(const MyMessage &message) {
//    receive_a0(message);
    //Serial.println("=== Node message received === ");
}*/

// code stored in the sketch: _3_Patio.ino
#define SN "Patio"                      // short Sketch (Node) name
#define SV "1.1"                        // short Sketch (Node) version
#define MY_NODE_ID 1                    // (1-254) to manually set Node ID

/* Includes
=========1=========2=========3=========4=========5=========6=========7========*/
#include "NRF24L01.h"                   // NRF24L01 definitions
#include <MySensors.h>                  // MySensors library
#include "s1.h"                         // DHT11 for Temperature and Humidity
#include "a1.h"                         // Relay for Spotlight

/* Presentation
=========1=========2=========3=========4=========5=========6=========7========*/
void presentation(){ 
    sendSketchInfo(SN, SV);             // Send the sketch version information
    // Register sensor(s) to gateway    // void present(uint8_t childSensorId, uint8_t sensorType, const char *description, bool ack);
    present(0, S_HUM,"Patio Humidity");             // present sensor to gateway
    present(1, S_TEMP,"Patio Temperature");         // present sensor to gateway
    present(2, S_BINARY,"Patio Spotlight");         // present sensor to gateway
    metric = getConfig().isMetric;                  // ???
    //Serial.println("=== Node presented === ");    // Debug
}

/* Setup
=========1=========2=========3=========4=========5=========6=========7========*/
void setup(){
    setup_a1();
    setup_s1();
    //Serial.println( "=== Node setup done ===" ); // Debug
}

/* Loop
=========1=========2=========3=========4=========5=========6=========7========*/
void loop(){
    loop_s1();
}

/* Receive
=========1=========2=========3=========4=========5=========6=========7========*/
void receive(const MyMessage &message) {
    receive_a1(message);
    //Serial.println("=== Node message received === "); // Debug
}

// code stored in the sketch: _4_Jacuzzi.ino
#define SN "Jacuzzi"                    // short Sketch (Node) name
#define SV "0.1"                        // short Sketch (Node) version
#define MY_NODE_ID 4                    // (1-254) to manually set Node ID

/* Includes
=========1=========2=========3=========4=========5=========6=========7========*/
#include "NRF24L01.h"                   // NRF24L01 definitions
#include <MySensors.h>                  // MySensors library

/* Presentation
=========1=========2=========3=========4=========5=========6=========7========*/
void presentation(){ 
    sendSketchInfo(SN, SV);             // Send the sketch version information
    // Register sensor(s) to gateway    // void present(uint8_t childSensorId, uint8_t sensorType, const char *description, bool ack);

    //Serial.println("=== Node presented === ");    // Debug
}

/* Setup
=========1=========2=========3=========4=========5=========6=========7========*/
void setup(){

    //Serial.println( "=== Node setup done ===" ); // Debug
}

/* Loop
=========1=========2=========3=========4=========5=========6=========7========*/
void loop(){

}

/* Receive
=========1=========2=========3=========4=========5=========6=========7========*/
void receive(const MyMessage &message) {

    //Serial.println("=== Node message received === "); // Debug
}

// code stored in the sketch: a0.h
/*
    Single Relay actuator for door lights

=========1=========2=========3=========4=========5=========6=========7========*/
MyMessage msg_a0(3, V_STATUS);          // define type of message sent to MySensors

/* Setup
=========1=========2=========3=========4=========5=========6=========7========*/
void setup_a0(){
    pinMode(relayPin, OUTPUT);         // set pin to output mode
}

/* Receive
=========1=========2=========3=========4=========5=========6=========7========*/
void receive_a0(const MyMessage &message){
    if (message.type==V_LIGHT) {       // We only expect one type of message from controller.
        digitalWrite(relayPin, message.getBool() ? 1 : 0);  // Toggle relay state
        // Serial.print("Toggle relay. New state is "); Serial.println(message.getBool());
   } 
}

/* ON
=========1=========2=========3=========4=========5=========6=========7========*/
void lightsOn(){
    if (pvState < 500) {               // only switch on if PV sensor says it's dark
        digitalWrite(relayPin, 1);     // switch off 
    }
}

/* OFF
=========1=========2=========3=========4=========5=========6=========7========*/
void lightsOff(int t){
    wait(t * 60 * 1000);               // wait for t minutes
    digitalWrite(relayPin, 0);         // then switch off 
}

// code stored in the sketch: a0.h.ino
/* Single Relay actuator
=========1=========2=========3=========4=========5=========6=========7========*/
const int relayPin = 3;                 // define switch pin
MyMessage msgRel(3, V_STATUS);          // define type of message sent to MySensors

/* Setup
=========1=========2=========3=========4=========5=========6=========7========*/
void setup_s3(){
    pinMode(3, OUTPUT);                     // set pin 3 in output mode
    /*digitalWrite(relayPin, loadState(3) ? 1 : 0);  // Set relay to last known state (using eeprom storage) */
}

/* Receive
=========1=========2=========3=========4=========5=========6=========7========*/
void receive_s3(const MyMessage &message){
    if (message.type==V_LIGHT) {                           // We only expect one type of message from controller.
        digitalWrite(relayPin, message.getBool() ? 1 : 0);  // Toggle relay state
        /*saveState(3, message.getBool());                // Store state in eeprom*/
        // Serial.print("Toggle relay. New state is "); Serial.println(message.getBool());
   } 
}

// code stored in the sketch: A1.h
/*
    Single Relay
*/

/* Initialize
=========1=========2=========3=========4=========5=========6=========7========*/
MyMessage msgA1(A1, V_STATUS);


/* Setup
=========1=========2=========3=========4=========5=========6=========7========*/
void setupA1(){
	// set relay pin in output mode
    pinMode(pinA1, OUTPUT);
	// load state from eeprom
	digitalWrite(pinA1, loadState(A1));
}


/* Receive
=========1=========2=========3=========4=========5=========6=========7========*/
void receiveA1(const MyMessage &message){
    if (message.type==V_STATUS) {
		// toggle relay state
		digitalWrite(pinA1,message.getBool());
		// save state to eeprom
		saveState(A1,message.getBool());
		// Printout
		Serial.println((String)"Toggle A1 relay. New state is "+message.getBool());
	}
}

// code stored in the sketch: A2.h
/*
    Single Relay actuator for door lights
    
    - should only switch the lights on if motion is detected and it's dark
    - should switch off by itself, 5 minutes after LAST motion was detected
*/

/* Initialize
=========1=========2=========3=========4=========5=========6=========7========*/
MyMessage msgA2(A2, V_STATUS);          // define type of message sent to MySensors

/* Setup
=========1=========2=========3=========4=========5=========6=========7========*/
void setupA2(){
    pinMode(pinA2, OUTPUT);         // set pin to output mode
}

/* Receive
=========1=========2=========3=========4=========5=========6=========7========*/
void receiveA2(const MyMessage &message){
    if (message.type == V_STATUS) {       // We only expect one type of message from controller.
        digitalWrite(pinA2, message.getBool() ? 1 : 0);  // Toggle relay state
        // Serial.print("Toggle relay. New state is "); Serial.println(message.getBool());
   } 
}

// code stored in the sketch: A3.h
/*
    InfraRed Receiver

    minus to gnd
    S to pin (the data pin must be PWM)
*/

/* Initialize
=========1=========2=========3=========4=========5=========6=========7========*/
MyMessage msgA3(A3, V_IR_SEND);
#include <IRremote.h>                   // the IR library
IRsend irsend;

/* Setup
=========1=========2=========3=========4=========5=========6=========7========*/
void setupA3(){
    pinMode(pinA3, OUTPUT);
}

/* Loop
=========1=========2=========3=========4=========5=========6=========7========*/
void loopA3(){}
/*
    Receive
=========1=========2=========3=========4=========5=========6=========7========*/
void receiveA3(const MyMessage &message){
	unsigned long sendCode = 0;
    if (message.type==V_IR_SEND) {
        Serial.print("Instruction Received: "); Serial.println( message.getString() );

		if ( strcmp(message.getString(), "brighter") == 0 ) 		{ sendCode = 0xFF3AC5; }
		else if ( strcmp(message.getString(), "darker") == 0 ) 		{ sendCode = 0xFFBA45; }
		else if ( strcmp(message.getString(), "play") == 0 )	 	{ sendCode = 0xFF827D; }
		else if ( strcmp(message.getString(), "power") == 0 ) 		{ sendCode = 0xFF02FD; }
		else if ( strcmp(message.getString(), "on") == 0 ) 			{ sendCode = 0xFF02FD; }
		else if ( strcmp(message.getString(), "off") == 0 ) 		{ sendCode = 0xFF02FD; }

		else if ( strcmp(message.getString(), "red") == 0 ) 		{ sendCode = 0xFF1AE5; }
		else if ( strcmp(message.getString(), "green") == 0 ) 		{ sendCode = 0xFF9A65; }
		else if ( strcmp(message.getString(), "blue") == 0 )	 	{ sendCode = 0xFFA25D; }
		else if ( strcmp(message.getString(), "white") == 0 ) 		{ sendCode = 0xFF22DD; }

		else if ( strcmp(message.getString(), "orange") == 0 ) 		{ sendCode = 0xFF2AD5; }
		else if ( strcmp(message.getString(), "lightgreen") == 0 ) 	{ sendCode = 0xFFAA55; }
		else if ( strcmp(message.getString(), "deepblue") == 0 ) 	{ sendCode = 0xFF926D; }
		else if ( strcmp(message.getString(), "milkwhite") == 0 ) 	{ sendCode = 0xFF12ED; }

		else if ( strcmp(message.getString(), "deepyellow") == 0 ) 	{ sendCode = 0xFF0AF5; }
		else if ( strcmp(message.getString(), "cyan") == 0 ) 		{ sendCode = 0xFF8A75; }
		else if ( strcmp(message.getString(), "bluepurple") == 0 ) 	{ sendCode = 0xFFB24D; }
		else if ( strcmp(message.getString(), "pinkwhite") == 0 ) 	{ sendCode = 0xFF32CD; }

		else if ( strcmp(message.getString(), "yellow") == 0 ) 		{ sendCode = 0xFF38C7; }
		else if ( strcmp(message.getString(), "lightblue") == 0 ) 	{ sendCode = 0xFFB847; }
		else if ( strcmp(message.getString(), "purple") == 0 ) 		{ sendCode = 0xFF7887; }
		else if ( strcmp(message.getString(), "greenwhite") == 0 ) 	{ sendCode = 0xFFF807; }

		else if ( strcmp(message.getString(), "lightyellow") == 0 ) { sendCode = 0xFF18E7; }
		else if ( strcmp(message.getString(), "skyblue") == 0 ) 	{ sendCode = 0xFF9867; }
		else if ( strcmp(message.getString(), "brown") == 0 ) 		{ sendCode = 0xFF58A7; }
		else if ( strcmp(message.getString(), "bluewhite") == 0 ) 	{ sendCode = 0xFFD827; }

		else if ( strcmp(message.getString(), "increasered") == 0 ) { sendCode = 0xFF28D7; }
		else if ( strcmp(message.getString(), "increasegreen") == 0){ sendCode = 0xFFA857; }
		else if ( strcmp(message.getString(), "increaseblue") == 0 ){ sendCode = 0xFF6897; }
		else if ( strcmp(message.getString(), "quicker") == 0 ) 	{ sendCode = 0xFFE817; }

		else if ( strcmp(message.getString(), "decreasered") == 0 )	{ sendCode = 0xFF08F7; }
		else if ( strcmp(message.getString(), "decreasegreen") == 0){ sendCode = 0xFF8877; }
		else if ( strcmp(message.getString(), "decreaseblue") == 0 ){ sendCode = 0xFF48B7; }
		else if ( strcmp(message.getString(), "slower") == 0 ) 		{ sendCode = 0xFFC837; }

		else if ( strcmp(message.getString(), "diy1") == 0 ) 		{ sendCode = 0xFF30CF; }
		else if ( strcmp(message.getString(), "diy2") == 0 ) 		{ sendCode = 0xFFB04F; }
		else if ( strcmp(message.getString(), "diy3") == 0 ) 		{ sendCode = 0xFF708F; }
		else if ( strcmp(message.getString(), "auto") == 0 ) 		{ sendCode = 0xFFF00F; }

		else if ( strcmp(message.getString(), "diy4") == 0 ) 		{ sendCode = 0xFF10EF; }
		else if ( strcmp(message.getString(), "diy5") == 0 ) 		{ sendCode = 0xFF906F; }
		else if ( strcmp(message.getString(), "diy6") == 0 ) 		{ sendCode = 0xFF50AF; }
		else if ( strcmp(message.getString(), "flash") == 0 ) 		{ sendCode = 0xFFD02F; }

		else if ( strcmp(message.getString(), "jump3") == 0 ) 		{ sendCode = 0xFF20DF; }
		else if ( strcmp(message.getString(), "jump7") == 0 ) 		{ sendCode = 0xFFA05F; }
		else if ( strcmp(message.getString(), "fade3") == 0 ) 		{ sendCode = 0xFF609F; }
		else if ( strcmp(message.getString(), "fade7") == 0 ) 		{ sendCode = 0xFFE01F; }

        Serial.print("Sending code: "); Serial.println( sendCode );
		irsend.sendNEC(sendCode,32);	// 32kHz carrier frequency for NEC
    }
}

// code stored in the sketch: def.h

/*  SENSORS
=========1=========2=========3=========4=========5=========6=========7========*/
#define A1              1               // Relay for BBQ floodlight
#define A3              2               // InfraRed transmitter 
#define S3T             3               // Temperature
#define S3B             4               // Pressure
#define S7              5               // Water Temperature
#define S8              6               // UV


/*  PINS & VARIABLES
=========1=========2=========3=========4=========5=========6=========7========*/

// A1 - Relay for BBQ floodlight
// -----------------------------
const int pinA1 =       2;              // the pin that the relay is atteched to
bool stateA1;                           // state of the button in the controller

// A3 - InfraRed transmitter - (RGB LED diode), to control the RGB strip
// -------------------------
const int pinA3 =       3;              // the data pin must be PWM

// S3 - Barometric Pressure
// ------------------------
const int pinS3sdl =    A4;             // data pin for SDL (data)
const int pinS3scl =    A5;             // data pin for SCL (clock)
unsigned long tS3 = 0;                  // will store last time loop fired
unsigned long iS3 = 5*60;               // interval at which to fire loop (seconds)

// S7 - Water temperature, a Dallas 
// ----------------------
const int pinS7 =       4;              // data pin
unsigned long tS7 = 0;                  // will store last time loop fired
unsigned long iS7 = 10*60;              // interval at which to fire loop (seconds)

// S8 - UV receiver
// ----------------
const int pinS8sdl =    A2;             // data pin for SDL (data)
const int pinS8scl =    A3;             // data pin for SCL (clock)
uint16_t valueS8 = 0;                   // reading the sensor status
unsigned long tS8 = 0;                  // will store last time loop fired
unsigned long iS8 = 5*60;               // interval at which to fire loop (seconds)
float uvIndex;
uint16_t uvIndexValue [12] = { 50, 227, 318, 408, 503, 606, 696, 795, 881, 976, 1079, 1170};

// code stored in the sketch: node02_BbqArea.ino
/**
    Sketch Information
=========1=========2=========3=========4=========5=========6=========7========*/
#define SN "BBQ Area"                   // short Sketch (Node) name
#define SV "1.1 17-12-12"               // short Sketch (Node) version
#define MY_NODE_ID 02                   // (1-254) to manually set Node ID
const bool Printout = true;             // set to false after testing

/**
    Library Includes
=========1=========2=========3=========4=========5=========6=========7========*/
#include "R.h"                          // NRF24L01 definitions
#include <MySensors.h>                  // MySensors library

/**
    Sensors and Activators
=========1=========2=========3=========4=========5=========6=========7========*/
    /**
     * A01 - Relay, BBQ gazebo light strip
     */
    #define A01                 1
    #define pinA01              2          
    bool stateA01;
    #include "A01_Relay_Inverted.h"

    /**
     * A03 - InfraRed transmitter for LED lights aroubd pool
     */
    #define A03                 2
    #define pinA03              3       // the data pin must be PWM
    #include "A03_IR_Remote.h"

    /**
     * S03 - Barometric Pressure and outside temperature
     */
    #define S03t                3       // Temperature
    #define S03b                4       // Pressure
    #define pinS03sdl          A4       // data pin for SDL (data)
    #define pinS03scl          A5       // data pin for SCL (clock)
    unsigned long tS03;                 // last time loop fired
    #include "S03_Barometer.h"

    /**
     * S07 - Water temperature, a Dallas
     */
    #define S07                 5       // Water Temperature
    #define pinS07              4       // data pin
    unsigned long tS07;                 // last time loop fired
    #include "S07_WaterTemp.h"          // Water temperature sensor

    /**
     * S8 - UV receiver
     */
    #define S08                 6       // UV
    #define pinS08sdl          A2       // data pin for SDL (data)
    #define pinS08scl          A3       // data pin for SCL (clock)
    unsigned long tS08;                 // last time loop fired
    #include "S08_UV.h"                 // UV sensor

/**
    Presentation
=========1=========2=========3=========4=========5=========6=========7========*/
void presentation() {
    sendSketchInfo(SN, SV);
    present(A01, S_BINARY, "BBQ Lights");
    present(A03, S_IR, "Poolside RGB Control");
    present(S03t, S_TEMP, "Poolside Temperature");
    present(S03b, S_BARO, "Poolside Barometer");
    present(S07, S_TEMP, "Water Temperature");
    present(S08, S_UV, "UV sensor");
    if (Printout==true) {Serial.println((String)" === Node "+MY_NODE_ID+" presented ("+SN+")"); }
}

/**
    Setup
=========1=========2=========3=========4=========5=========6=========7========*/
void setup() {
    setupA01();
    setupA03();
    setupS03();
    setupS07();
    setupS08();
    if (Printout==true) {Serial.println((String)" === Node "+MY_NODE_ID+" setup ("+SN+")"); }
}

/**
    Loop
=========1=========2=========3=========4=========5=========6=========7========*/
void loop() {
    loopS03(300);                       // every 5 minutes (300) seconds
    loopS07(300);
    loopS08(300);
}

/**
    Receive
=========1=========2=========3=========4=========5=========6=========7========*/
void receive(const MyMessage &message) {
    receiveA01(message);
    receiveA03(message);
}

// code stored in the sketch: NRF24L01.h
/* NRF24L01 defintions
=========1=========2=========3=========4=========5=========6=========7========*/
//#define MY_DEBUG                              // Enable debug prints to serial monitor
//#define MY_DEBUG_VERBOSE_RF24                 // Enable for verbose debug prints related to the RF24 driver. Requires DEBUG to be enabled.

#define MY_RADIO_NRF24                          // Enable if you want to use a NRF24L01+ radio
#define MY_REPEATER_FEATURE                     // Enables repeater functionality (relays messages from other nodes).

#define MY_RF24_PA_LEVEL RF24_PA_MAX            // Set radio power (Options are: _MIN, _LOW, _HIGH or _MAX)
#define MY_RF24_DATARATE RF24_250KBPS           // Set radio transmission rate

/* Optional & Additional
=========1=========2=========3=========4=========5=========6=========7========*/
//#define MY_RF24_CHANNEL 76                    // Change radio channel, has to be done on all nodes

//#define MY_SIGNING_ATSHA204                   // Enables hardware signing using ATSHA204
//#define MY_SIGNING_SOFT                       // Enables software signing

//#define MY_PARENT_NODE_ID                             
//#define MY_PARENT_NODE_IS_STATIC

//#define MY_DISABLED_SERIAL                    // Enable if you want to use TX(1), RX(0) as normal I/O pin
//#define MY_RF24_ENABLE_ENCRYPTION

// code stored in the sketch: R.h
/* 
    NRF24L01 defintions

=========1=========2=========3=========4=========5=========6=========7========*/
//#define MY_DEBUG                              // Enable debug prints to serial monitor
//#define MY_DEBUG_VERBOSE_RF24                 // Enable for verbose debug prints related to the RF24 driver. Requires DEBUG to be enabled.

#define MY_RADIO_NRF24                          // Enable if you want to use a NRF24L01+ radio
#define MY_REPEATER_FEATURE                     // Enables repeater functionality (relays messages from other nodes).

#define MY_RF24_PA_LEVEL RF24_PA_MAX            // Set radio power (Options are: _MIN, _LOW, _HIGH or _MAX)
#define MY_RF24_DATARATE RF24_250KBPS           // Set radio transmission rate

/* Optional & Additional
=========1=========2=========3=========4=========5=========6=========7========*/
//#define MY_RF24_CHANNEL 76                    // Change radio channel, has to be done on all nodes

//#define MY_SIGNING_ATSHA204                   // Enables hardware signing using ATSHA204
//#define MY_SIGNING_SOFT                       // Enables software signing

//#define MY_PARENT_NODE_ID                     // Gateway is 0
//#define MY_PARENT_NODE_IS_STATIC

//#define MY_DISABLED_SERIAL                    // Enable if you want to use TX(1), RX(0) as normal I/O pin
//#define MY_RF24_ENABLE_ENCRYPTION

// code stored in the sketch: s0.h
/* 
    Passive InfraRed Switch

=========1=========2=========3=========4=========5=========6=========7========*/
MyMessage msg_s0(0, V_TRIPPED);        // define type of message sent to MySensors

/* Setup
=========1=========2=========3=========4=========5=========6=========7========*/
void setup_s0(){
    pinMode(pirPin, INPUT);            // initialize sensor as an input
}

/* Loop
=========1=========2=========3=========4=========5=========6=========7========*/
void loop_s0(){
    pirVal = digitalRead(pirPin);               // read and store sensor value
    //Serial.print("PIR is at: "); Serial.println(pirVal);
    if (pirVal == HIGH && pirState == LOW) {    // check if the sensor is tripped
        Serial.println("-----> Motion detected!");
        pirState = HIGH;       	                // update variable state to HIGH
        pirTimer ++;
//        lightsOn();                           // Switch on lights
    }
    if (pirState == HIGH && pirTimer>60){
        pirState = LOW;                           // update variable state to LOW
        pirTimer=0;
//        lightsOff(5);                         // Set timer to switch off light 5 minutes
    }
    send(msg_s0.set(pirVal ? "1" : "0"));       // Send tripped value to gw
}

// code stored in the sketch: s1.h
/*
    Reed Switch

=========1=========2=========3=========4=========5=========6=========7========*/
MyMessage msg_s1(1, V_TRIPPED);        // define type of message sent to MySensors

/* Setup
=========1=========2=========3=========4=========5=========6=========7========*/
void setup_s1(){
    pinMode(reedPin, INPUT);           // initialize sensor as an input
}

/* Loop
=========1=========2=========3=========4=========5=========6=========7========*/
void loop_s1(){
    reedVal = digitalRead(reedPin);   	 // read and store sensor value
    //Serial.print("Reed is at: "); Serial.println(reedVal);
    if (reedVal == HIGH) {        // check if the sensor is tripped
        Serial.println("Your Door is Closed");
    } else {
        Serial.println("Your Door is Open");
    }
    send(msg_s1.set(reedVal ? "0" : "1"));       // Send tripped value to gw
}

// code stored in the sketch: s2.h
/*
    PhotoVoltaic Sensor

=========1=========2=========3=========4=========5=========6=========7========*/
MyMessage msg_s2(2, V_LIGHT_LEVEL);    // define type of message sent to MySensors

/* Setup
=========1=========2=========3=========4=========5=========6=========7========*/
void setup_s2(){
    pinMode(pvPin, INPUT);             // initialize sensor as an input
}

/* Loop
=========1=========2=========3=========4=========5=========6=========7========*/
void loop_s2(){
    pvVal = analogRead(pvPin);   	   // read and store sensor value
    Serial.print("Light is at: "); Serial.println(pvVal);
    if (pvState != pvVal){             // if the state has changed
        pvState = pvVal;               // update state
        //  send message to mycontroller
        send(msg_s2.set(pvVal));
    }
}

/*
    // a few threshholds, qualitatively determined
    if (pvVal < 10) {
        Serial.println(" - Dark");
    } else if (pvVal < 200) {
        Serial.println(" - Dim");
    } else if (pvVal < 500) {
        Serial.println(" - Light");
    } else if (pvVal < 800) {
        Serial.println(" - Bright");
    } else {
        Serial.println(" - Very bright");
    }
 */

// code stored in the sketch: S3.h
/*
    Barometric Pressure Sensor
*/


/*  LIBRARIES
=========1=========2=========3=========4=========5=========6=========7========*/
#include <Wire.h>                      // include libraries
#include "Adafruit_BMP085.h"
Adafruit_BMP085 bmp;

/* Initialize
=========1=========2=========3=========4=========5=========6=========7========*/
MyMessage msgS3T(S3T, V_TEMP);          // message sent to MySensors
MyMessage msgS3B(S3B, V_PRESSURE);      // message sent to MySensors


/* Setup
=========1=========2=========3=========4=========5=========6=========7========*/
void setupS3(){
    if( !bmp.begin()){
        Serial.println("~~~ bmp has a problem ~~~" );
    }
}


/* Loop
=========1=========2=========3=========4=========5=========6=========7========*/
void loopS3(){
	if( millis() - tS3 > iS3*1000 ) {
		tS3 = millis();        			// save the last time this fired
		Serial.print("Temperature = "); Serial.print(bmp.readTemperature()); Serial.println(" C");
		send(msgS3T.set( bmp.readTemperature(),2 ));
		Serial.print("Pressure = "); Serial.print(bmp.readPressure()/100); Serial.println(" Pa");
		send(msgS3B.set( bmp.readPressure()/100,2 ));
		Serial.println();
	}
}

// code stored in the sketch: S4.h
/* 
    Passive InfraRed Switch
	
*/

/* Initialize
=========1=========2=========3=========4=========5=========6=========7========*/
MyMessage msgS4(S4, V_TRIPPED);        // type of message sent to MySensors

/* Setup
=========1=========2=========3=========4=========5=========6=========7========*/
void setupS4(){
    pinMode(pinS4, INPUT);             // initialize sensor as an input
	stateS4 = request(S4, V_TRIPPED);  // get status from controller
    digitalWrite(pinS4, stateS4);      // turn on/off based on controller state

}

/* Loop
=========1=========2=========3=========4=========5=========6=========7========*/
void loopS4(){
	valueS4 = digitalRead(pinS4);       // Read the state of the switch
	if (valueS4 != stateS4) {           // If different from last state
        if (valueS4 == 0){              // Pin reads low
			Serial.println((String)"- Standing down after "+ ((millis()-tS4)/1000) + " seconds");
        } else if (valueS4 == 1){
			tS4 = millis();				// time when loop fired (for calibrating the timer)
			Serial.println("--- Motion detected! --- ");
        }
        send(msgS4.set(valueS4));       // send to controller
        stateS4 = valueS4;              // update state
		wait(2000);						// wait 2 seconds so it doesnt bounce
    }
}

// code stored in the sketch: S5.h
/*
    Water Temperature
*/

/* Initialize
=========1=========2=========3=========4=========5=========6=========7========*/
MyMessage msgS5(S5, V_TEMP);
#include <OneWire.h>
#include <DallasTemperature.h>

// Setup a oneWire instance to communicate with any OneWire devices
OneWire oneWire(pinS5);

// Pass our oneWire reference to Dallas Temperature.
DallasTemperature sensors(&oneWire);

/* Setup
=========1=========2=========3=========4=========5=========6=========7========*/
void setupS5(){
    pinMode(pinS5, INPUT_PULLUP);      // initialize sensor as an pullup input
    sensors.begin();                   // Start up the library
    Serial.print("Found "); Serial.print(sensors.getDeviceCount()); Serial.println(" devices.");
}


/* Loop
=========1=========2=========3=========4=========5=========6=========7========*/
void loopS5(){
    sensors.requestTemperatures();     // Send the command to get temperatures
    Serial.print("Temperature for waterproof sensor (0) is: ");
    float valueS5 = sensors.getTempCByIndex(0);       // 0 refers to the first IC on the wire
    Serial.println(valueS5);
}

// code stored in the sketch: S6.h
/*
    UV Sensor

*/

/* Initialize
=========1=========2=========3=========4=========5=========6=========7========*/
MyMessage msgS6(S6, V_UV);

/* Setup
=========1=========2=========3=========4=========5=========6=========7========*/
void setupS6(){
    pinMode(pinS6, INPUT);           // initialize sensor as an input
}

/* Loop
=========1=========2=========3=========4=========5=========6=========7========*/
void loopS6(){
    
}

// code stored in the sketch: S7.h
/*
    Water Temperature

		- Vktech DS18b20 Waterproof Temperature Sensors

		- You will need a pull-up resistor of about 5 KOhm between the 1-Wire data line and your 5V power.
		- If you are using the DS18B20, ground pins 1 and 3. The centre pin is the data line '1-wire'.

*/

/* Initialize
=========1=========2=========3=========4=========5=========6=========7========*/
MyMessage msgS7(S7, V_TEMP);
#include <OneWire.h>
#include <DallasTemperature.h>

OneWire oneWire(pinS7);																											// Setup a oneWire instance to communicate with any OneWire devices

DallasTemperature sensors(&oneWire);																					// Pass our oneWire reference to Dallas Temperature.

/* Setup
=========1=========2=========3=========4=========5=========6=========7========*/
void setupS7(){
	Serial.begin(9600); 			//Begin serial communication at 9600
    pinMode(pinS7, INPUT);      																						// initialize sensor as an pullup input
    sensors.begin();                   																			// Start up the library
    Serial.print("Found "); Serial.print(sensors.getDeviceCount()); Serial.println(" devices.");
}

/* Loop
=========1=========2=========3=========4=========5=========6=========7========*/
void loopS7(){
	if( millis() - tS7 > iS7*1000 ) {
		tS7 = millis();        																									// save the last time this fired
		sensors.requestTemperatures();  																				// Send the command to get temperatures
		Serial.print("Temperature for waterproof sensor (0) is: ");
		Serial.println(sensors.getTempCByIndex(0));															// 0 refers to the first IC on the wire
		send(msgS7.set( sensors.getTempCByIndex(0),2 ));
	}
}

// code stored in the sketch: S8.h
/*
    UV Sensor

*/

/* Initialize
=========1=========2=========3=========4=========5=========6=========7========*/
MyMessage msgS8(S8, V_UV);    			// define type of message sent to MySensors

/* Setup
=========1=========2=========3=========4=========5=========6=========7========*/
void setupS8(){
    pinMode(pinS8sdl, INPUT);           // initialize sensor as an input
}

/* Loop
=========1=========2=========3=========4=========5=========6=========7========*/
void loopS8(){
	if( millis() - tS8 > iS8*1000 ) {
		tS8 = millis();        			// save the last time this fired
		valueS8 = analogRead(pinS8sdl);	// Get UV value
		if (valueS8>1170) {valueS8=1170;}
		Serial.print("UV Analog reading: "); Serial.println(valueS8);
		int i;
		for (i = 0; i < 12; i++){
			if (valueS8 <= uvIndexValue[i]){
				uvIndex = i;
				break;
			}
		}
		//calculate 1 decimal if possible
		if (i>0) {
			float vRange = uvIndexValue[i] - uvIndexValue[i-1];
			float vCalc = valueS8 - uvIndexValue[i-1];
			uvIndex+=(1.0/vRange)*vCalc-1.0;
		}
		Serial.print("UVI: "); Serial.println(uvIndex,2);
		send(msgS8.set(uvIndex,2));
	}
}

// code stored in the sketch: X.h
/* LED STRIP IR REMOTE CODES
=========1=========2=========3=========4=========5=========6=========7========*/
/*
01. 16726725 / 3017062527
02. 16759365 / 1145637499
03. 16745085 / 831890207
04. 16712445 / 

05. 16718565 (red)
06. 16751205 (green)
07. 16753245 (blue)
08. 16720605 (white)

09. 16722645 / 1535358491 (orange)
10. 16755285 / 3039890975 (light green)
11. 16749165 / 3302114724 (deep blue)
12. 16716525 / 3814356023 (milk white)

13. 16714485 / 2962012127 (deep yellow)
14. 16747125 / 1090587099 (cyan)
15. 16757325 / 2126716663 (blue-purple)
16. 16724685 / 3998141691 (pink white)

17. 16726215 / 1217346747 (yellow)
18. 16758855 / 2721879231 (light blue)
19. 16742535 / 4131161687 (purple)
20. 16775175 / 3877748955 (green white)

21. 16718055 / 1033561079 (light yellow)
22. 16750695 / 2538093563 (sky blue)
23. 16734375 / 3691091931 (brown)
24. 16767015 / 2259740311 (blue white)

25. (increase red)
26. (increase green)
27. (increase blue)
28. (quicker)

29. (decrease red)
30. (decrease green)
31. (decrease blue)
32. (slower)

33. (diy 1)
34. (diy 2)
35. (diy 3)
36. (auto color change)

37. (diy 4)
38. (diy 5)
39. (diy 6)
40. (flash)

41. (jump 3)
42. (jump 7)
43. (fade 3)
44. (fade 7)

.. long press 4294967295
*/

// code stored in the sketch: xxx.h
/*
    FRONT DOOR

    RADIO
repeater

    SENSORS
PIR switch - to check if someone is in front of the door
Reed switch - to sense if door is open or closed
Photovoltaic sensor -  to check if it's day or night
? Electric lock - status if door is locked

    ACTUATORS
Relay, to switch on the lights
? Lock/Unlock via electrick lock

*/

// code stored in the sketch: zzz.h

/*       ACTUATORS
=========1=========2=========3=========4=========5=========6=========7========*/

// Relay for BBQ floodlight
#define A1          1                   // Sensor number
const int pinA1 =   2;                  // the pin that the relay is atteched to

// InfraRed transmitter (RGB LED diode), to control the RGB strip
#define A3          2                   // Sensor number
const int pinA3 =   3;                  // the pin that the relay is atteched to


/*      SENSORS
=========1=========2=========3=========4=========5=========6=========7========*/

// Barometric Pressure
// -------------------
#define S3_1        3                   // Sensor number
#define S3_2        4                   // Sensor number
const int pinS3_1 = A4;                 // data pin for SDL (data)
const int pinS3_2 = A5;                 // data pin for SCL (clock)

// PIR switch
// ----------
#define S4          5                   // Sensor number
const int pinS4 =   5;                  // data pin
int valueS4 = 0;                        // variable for reading the sensor status
int stateS4 = 0;                        // variable for storing the last state
int countS4 = 0;                        // variable to store the number of loops

// Water temperature
// -----------------
#define S5          6                   // Sensor number
const int pinS5 =   6;                  // data pin
float valueS5;                          // variable for reading the sensor status

// UV receiver
// -----------
#define S6          7                   // Sensor number
const int pinS6 =   7;                 // data pin
int valueS6 = 0;                        // variable for reading the sensor status
int stateS6 = 0;                        // variable for storing the last state
