# Fritzing sketch node07_Kitchen (saved by Fritzing 0.9.3b)
circuit board: 6cm x 4cm
perfboards: 2

parts:
  HLK-PM1 = HLK-PM01
  Part5 = Arduino Nano (Rev3.0)
  U2 = SWITCH-SPST-2 [package=switch-spst-vertical]
  Part6 = NRF24L01+ Breakout Board
  Power_plug1 = Power plug
  J1 = screw terminal, 2 pins  # not connected
  KY-1 = Keyes Relay [part_number=A1 package=THT]
  S1 = SWITCH-MOMENTARY-2 [part_number=S1 package=reed_switch_pth]
  U3 = GAS_SENSOR [package=mq-3]

nets:
  N1: HLK-PM1.AC#0, U2.P
  N2: HLK-PM1.AC#1, Power_plug1.GND
  GND: Part5.GND, Part6.GND, KY-1.ground, S1.1, U3.H2
  N3: Part5.D2, KY-1.signal
  N4: Part5.D3, S1.2
  N5: Part5.D9, Part6.CE
  N6: Part5.D10, Part6.CS
  N7: Part5.D11/MOSI, Part6.MOSI
  N8: Part5.D12/MISO, Part6.MISO
  N9: Part5.5V, KY-1.power, U3.H1
  N10: Part5.A0, U3.A1
  3V3: Part5.3V3, Part6.VCC
  N11: Part5.D13/SCK, Part6.SCK
  N12: U2.O, Power_plug1.VCC

custom parts:
  Keyes Relay: The Keyes 5V relay module is suitable for SCM development, home appliance control. It uses a 5V~12V TIL control signal which can control DC / AC signal.

// code stored in the sketch: _1_FrontDoor.ino

#define SN "Front Door"                 // short Sketch name
#define SV "0.9"                        // short Sketch version
#define MY_NODE_ID 1                    // (1-254) to manually set Node ID

/* Includes
=========1=========2=========3=========4=========5=========6=========7========*/
#include "NRF24L01.h"                   // NRF24L01 definitions
#include <MySensors.h>                  // MySensors library
#include "zzz.h"                        // Explanation and inital variables

//#include "a0.h"                         // Relay, to switch on the lights when needed
//#include "a1.h"                         // Lock and unlock the front door

#include "s0.h"                         // PIR switch, check if someone is in front of the door
#include "s1.h"                         // Reed switch, check if door is open or closed
#include "s2.h"                         // Photovoltaic sensor, to check if it's dark

/* Presentation
=========1=========2=========3=========4=========5=========6=========7========*/
void presentation(){ 
    sendSketchInfo(SN, SV);             // Send the sketch version information
    // Register the sensor(s) to the controller
    /* void present(uint8_t childSensorId, uint8_t sensorType, const char *description, bool ack); */
    present(0, S_MOTION, "PIR switch");
    present(1, S_DOOR, "Reed switch");
    present(2, S_LIGHT_LEVEL, "PV switch");
//    present(3, S_BINARY, "Lights relay");
    //Serial.println("=== Node presented === ");
}

/* Setup
=========1=========2=========3=========4=========5=========6=========7========*/
void setup() {
    setup_s0();
    setup_s1();
    setup_s2();
//    setup_a0();
    //Serial.println( "=== Node setup done ===" );
}

/* Loop
=========1=========2=========3=========4=========5=========6=========7========*/
void loop() {
    loop_s0();
    loop_s1();
    loop_s2();
    wait(2000);                         // wait a bit, loop once every 2 seconds
}

/* Receive
=========1=========2=========3=========4=========5=========6=========7========*/
/*void receive(const MyMessage &message) {
//    receive_a0(message);
    //Serial.println("=== Node message received === ");
}*/

// code stored in the sketch: _3_Patio.ino
#define SN "Patio"                      // short Sketch (Node) name
#define SV "1.1"                        // short Sketch (Node) version
#define MY_NODE_ID 1                    // (1-254) to manually set Node ID

/* Includes
=========1=========2=========3=========4=========5=========6=========7========*/
#include "NRF24L01.h"                   // NRF24L01 definitions
#include <MySensors.h>                  // MySensors library
#include "s1.h"                         // DHT11 for Temperature and Humidity
#include "a1.h"                         // Relay for Spotlight

/* Presentation
=========1=========2=========3=========4=========5=========6=========7========*/
void presentation(){ 
    sendSketchInfo(SN, SV);             // Send the sketch version information
    // Register sensor(s) to gateway    // void present(uint8_t childSensorId, uint8_t sensorType, const char *description, bool ack);
    present(0, S_HUM,"Patio Humidity");             // present sensor to gateway
    present(1, S_TEMP,"Patio Temperature");         // present sensor to gateway
    present(2, S_BINARY,"Patio Spotlight");         // present sensor to gateway
    metric = getConfig().isMetric;                  // ???
    //Serial.println("=== Node presented === ");    // Debug
}

/* Setup
=========1=========2=========3=========4=========5=========6=========7========*/
void setup(){
    setup_a1();
    setup_s1();
    //Serial.println( "=== Node setup done ===" ); // Debug
}

/* Loop
=========1=========2=========3=========4=========5=========6=========7========*/
void loop(){
    loop_s1();
}

/* Receive
=========1=========2=========3=========4=========5=========6=========7========*/
void receive(const MyMessage &message) {
    receive_a1(message);
    //Serial.println("=== Node message received === "); // Debug
}

// code stored in the sketch: a0.h
/*
    Single Relay actuator for door lights

=========1=========2=========3=========4=========5=========6=========7========*/
MyMessage msg_a0(3, V_STATUS);          // define type of message sent to MySensors

/* Setup
=========1=========2=========3=========4=========5=========6=========7========*/
void setup_a0(){
    pinMode(relayPin, OUTPUT);         // set pin to output mode
}

/* Receive
=========1=========2=========3=========4=========5=========6=========7========*/
void receive_a0(const MyMessage &message){
    if (message.type==V_LIGHT) {       // We only expect one type of message from controller.
        digitalWrite(relayPin, message.getBool() ? 1 : 0);  // Toggle relay state
        // Serial.print("Toggle relay. New state is "); Serial.println(message.getBool());
   } 
}

/* ON
=========1=========2=========3=========4=========5=========6=========7========*/
void lightsOn(){
    if (pvState < 500) {               // only switch on if PV sensor says it's dark
        digitalWrite(relayPin, 1);     // switch off 
    }
}

/* OFF
=========1=========2=========3=========4=========5=========6=========7========*/
void lightsOff(int t){
    wait(t * 60 * 1000);               // wait for t minutes
    digitalWrite(relayPin, 0);         // then switch off 
}

// code stored in the sketch: a0.h.ino
/* Single Relay actuator
=========1=========2=========3=========4=========5=========6=========7========*/
const int relayPin = 3;                 // define switch pin
MyMessage msgRel(3, V_STATUS);          // define type of message sent to MySensors

/* Setup
=========1=========2=========3=========4=========5=========6=========7========*/
void setup_s3(){
    pinMode(3, OUTPUT);                     // set pin 3 in output mode
    /*digitalWrite(relayPin, loadState(3) ? 1 : 0);  // Set relay to last known state (using eeprom storage) */
}

/* Receive
=========1=========2=========3=========4=========5=========6=========7========*/
void receive_s3(const MyMessage &message){
    if (message.type==V_LIGHT) {                           // We only expect one type of message from controller.
        digitalWrite(relayPin, message.getBool() ? 1 : 0);  // Toggle relay state
        /*saveState(3, message.getBool());                // Store state in eeprom*/
        // Serial.print("Toggle relay. New state is "); Serial.println(message.getBool());
   } 
}

// code stored in the sketch: A1.h
/*
    Single Relay
*/

/* Initialize
=========1=========2=========3=========4=========5=========6=========7========*/
MyMessage msgA1(A1, V_STATUS);


/* Setup
=========1=========2=========3=========4=========5=========6=========7========*/
void setupA1(){
    pinMode(pinA1, OUTPUT);             		// set relay pin in output mode
	digitalWrite(pinA1, loadState(A1)); 		// load state from eeprom
}


/* Receive
=========1=========2=========3=========4=========5=========6=========7========*/
void receiveA1(const MyMessage &message){
    if (message.type==V_STATUS) {
		digitalWrite(pinA1, message.getBool()); // toggle relay state
		saveState(A1,message.getBool());		// save state to eeprom
		Serial.println((String)"Toggle relay. New state is "+message.getBool());
	}
}

// code stored in the sketch: def.h

/*  SENSORS
=========1=========2=========3=========4=========5=========6=========7========*/
#define A1              1               // Relay
#define S1              2               // Reed switch
#define S14             3               // MQ2 (Gas/Smoke)


/*  PINS & VARIABLES
=========1=========2=========3=========4=========5=========6=========7========*/

// A1 - Relay for lights
// ---------------------
const int pinA1 =       2;              // the pin that the relay is atteched to

// S1 - Reed switch - pantry
// -----------------------
const int pinS1 =       3;              // data pin with pull-up resistor
int valueS1 = 0;                        // reading the sensor status
int stateS1 = 0;                        // storing the last state

// S14 - Gas/Smoke
// -----------------------
const int pinS14 =     A0;             // data pin
#define         RL_VALUE                     (5)     //define the load resistance on the board, in kilo ohms
#define         RO_CLEAN_AIR_FACTOR          (9.83)  //RO_CLEAR_AIR_FACTOR=(Sensor resistance in clean air)/RO, which is derived from the chart in datasheet
#define         CALIBARAION_SAMPLE_TIMES     (50)    //define how many samples you are going to take in the calibration phase
#define         CALIBRATION_SAMPLE_INTERVAL  (500)   //define the time interal(in milisecond) between each samples in the calibration phase
#define         READ_SAMPLE_INTERVAL         (50)    //define how many samples you are going to take in normal operation
#define         READ_SAMPLE_TIMES            (5)     //define the time interal(in milisecond) between each samples in normal operation
#define         GAS_LPG                      (0)
#define         GAS_CO                       (1)
#define         GAS_SMOKE                    (2)
float Ro = 10000.0;    // this has to be tuned 10K Ohm
int valueS14 = 0;           // variable to store the value coming from the sensor
float valMQ =0.0;
float lastMQ =0.0;
float LPGCurve[3]  =  {2.3,0.21,-0.47};   //two points are taken from the curve. with these two points, a line is formed which is "approximately equivalent" to the original curve.
//data format:{ x, y, slope}; point1: (lg200, 0.21), point2: (lg10000, -0.59)
float COCurve[3]  =  {2.3,0.72,-0.34};    //two points are taken from the curve. with these two points, a line is formed which is "approximately equivalent" to the original curve.
//data format:{ x, y, slope}; point1: (lg200, 0.72), point2: (lg10000,  0.15)
float SmokeCurve[3] = {2.3,0.53,-0.44};   //two points are taken from the curve. with these two points, a line is formed which is "approximately equivalent" to the original curve.
//data format:{ x, y, slope}; point1: (lg200, 0.53), point2:(lg10000,-0.22)

// code stored in the sketch: node06_Garage.ino
#define SN "Garage"                     // short Sketch (Node) name
#define SV "1.1"                        // short Sketch (Node) version
#define MY_NODE_ID 6                    // (1-254) to manually set Node ID
/*
    Includes
=========1=========2=========3=========4=========5=========6=========7========*/
#include "R.h"                          // NRF24L01 definitions
#include <MySensors.h>                  // MySensors library
#include "def.h"                        // Explanation and inital variables
  #include "A1.h"                       // Relay - lights
  #include "S1.h"                       // Reed - gate
  #include "S4.h"                       // PIR
  #include "S13.h"                      // UltraSonic
/*
    Presentation
=========1=========2=========3=========4=========5=========6=========7========*/
void presentation(){ 
  sendSketchInfo(SN, SV);
    present(A1, S_BINARY, "Garage Lights");
    present(S1, S_DOOR, "Garage Gate");
    present(S4, S_MOTION, "Garage PIR");
    present(S13, S_DISTANCE, "Garage Parking");
  Serial.println((String)" === Node "+MY_NODE_ID+" presented ("+SN+")");
}
/* 
    Setup
=========1=========2=========3=========4=========5=========6=========7========*/
void setup(){
    setupA1();
    setupS1();
    setupS4();
    setupS13();
  Serial.println((String)" === Node "+MY_NODE_ID+" setup ("+SN+")");
}
/*
    Loop
=========1=========2=========3=========4=========5=========6=========7========*/
void loop(){
    loopS1();
    loopS4();
    loopS13();
  wait(1000);
}
/*
    Receive
=========1=========2=========3=========4=========5=========6=========7========*/
void receive(const MyMessage &message) {
    receiveA1(message);
}

// code stored in the sketch: node07_Kitchen.ino
#define SN "Kitchen"                    // short Sketch (Node) name
#define SV "1.1"                        // short Sketch (Node) version
#define MY_NODE_ID 7                    // (1-254) to manually set Node ID
/*
    Includes
=========1=========2=========3=========4=========5=========6=========7========*/
#include "R.h"                          // NRF24L01 definitions
#include <MySensors.h>                  // MySensors library
#include "def.h"                        // Explanation and inital variables
  #include "A1.h"                       // Relay - pantry lights
  #include "S1.h"                       // Reed - pantry door
  #include "S14.h"                      // MQ2 - gas and smoke
/*
    Presentation
=========1=========2=========3=========4=========5=========6=========7========*/
void presentation(){ 
  sendSketchInfo(SN, SV);
    present(A1, S_BINARY, "Pantry Lights");
    present(S1, S_DOOR, "Pantry Door");
    present(S14, S_AIR_QUALITY, "Gas Detection");
  Serial.println((String)" === Node "+MY_NODE_ID+" presented ("+SN+")");
}
/*
    Setup
=========1=========2=========3=========4=========5=========6=========7========*/
void setup(){
    setupA1();
    setupS1();
    setupS14();
  Serial.println((String)" === Node "+MY_NODE_ID+" setup ("+SN+")");
}
/*
    Loop
=========1=========2=========3=========4=========5=========6=========7========*/
void loop(){
    loopS1();
    loopS14();
  wait(1000);
}
/*
Receive
=========1=========2=========3=========4=========5=========6=========7========*/
void receive(const MyMessage &message) {
    receiveA1(message);
}

// code stored in the sketch: R.h
/* 
    NRF24L01 defintions

=========1=========2=========3=========4=========5=========6=========7========*/
//#define MY_DEBUG                              // Enable debug prints to serial monitor
//#define MY_DEBUG_VERBOSE_RF24                 // Enable for verbose debug prints related to the RF24 driver. Requires DEBUG to be enabled.

#define MY_RADIO_NRF24                          // Enable if you want to use a NRF24L01+ radio
#define MY_REPEATER_FEATURE                     // Enables repeater functionality (relays messages from other nodes).

#define MY_RF24_PA_LEVEL RF24_PA_MAX            // Set radio power (Options are: _MIN, _LOW, _HIGH or _MAX)
#define MY_RF24_DATARATE RF24_250KBPS           // Set radio transmission rate

/* Optional & Additional
=========1=========2=========3=========4=========5=========6=========7========*/
//#define MY_RF24_CHANNEL 76                    // Change radio channel, has to be done on all nodes

//#define MY_SIGNING_ATSHA204                   // Enables hardware signing using ATSHA204
//#define MY_SIGNING_SOFT                       // Enables software signing

//#define MY_PARENT_NODE_ID                     // Gateway is 0
//#define MY_PARENT_NODE_IS_STATIC

//#define MY_DISABLED_SERIAL                    // Enable if you want to use TX(1), RX(0) as normal I/O pin
//#define MY_RF24_ENABLE_ENCRYPTION

// code stored in the sketch: s0.h
/* 
    Passive InfraRed Switch

=========1=========2=========3=========4=========5=========6=========7========*/
MyMessage msg_s0(0, V_TRIPPED);        // define type of message sent to MySensors

/* Setup
=========1=========2=========3=========4=========5=========6=========7========*/
void setup_s0(){
    pinMode(pirPin, INPUT);            // initialize sensor as an input
}

/* Loop
=========1=========2=========3=========4=========5=========6=========7========*/
void loop_s0(){
    pirVal = digitalRead(pirPin);               // read and store sensor value
    //Serial.print("PIR is at: "); Serial.println(pirVal);
    if (pirVal == HIGH && pirState == LOW) {    // check if the sensor is tripped
        Serial.println("-----> Motion detected!");
        pirState = HIGH;       	                // update variable state to HIGH
        pirTimer ++;
//        lightsOn();                           // Switch on lights
    }
    if (pirState == HIGH && pirTimer>60){
        pirState = LOW;                           // update variable state to LOW
        pirTimer=0;
//        lightsOff(5);                         // Set timer to switch off light 5 minutes
    }
    send(msg_s0.set(pirVal ? "1" : "0"));       // Send tripped value to gw
}

// code stored in the sketch: S1.h
/* 
    Reed Switch

 - Since one end of the reed switch is connected to ground, we need to pull-up the reed switch pin internally
 - Use Arduino’s internal pull-up resistor to bias the switch high
 - This effectively inverts the behavior of the INPUT mode, where HIGH means the sensor is off, and LOW means the sensor is on.
 - So, when the switch closes, it will connect pin 2 directly to ground, and it should read low
*/

/*
    Initialize
=========1=========2=========3=========4=========5=========6=========7========*/
MyMessage msgS1(S1, V_TRIPPED);         // type of message sent to MySensors
/*
    Setup
=========1=========2=========3=========4=========5=========6=========7========*/
void setupS1(){
    pinMode(pinS1, INPUT);       		// pull-up the pin internally
}
/* 
    Loop
=========1=========2=========3=========4=========5=========6=========7========*/
void loopS1(){
    valueS1 = digitalRead(pinS1);       // Read the state of the switch
    if (valueS1 != stateS1) {           // If different from last state
        if (valueS1 == 0){              // Pin reads low, the door is closed.
            Serial.println("S1 is Closed (Untripped)");
        } else if (valueS1 == 1){
            Serial.println("S1 is Open (Tripped)");
        }
        send(msgS1.set(valueS1));       // send to controller
        stateS1 = valueS1;              // update state
    }
}
/*
    Receive
=========1=========2=========3=========4=========5=========6=========7========*/
// nothing to receive

// code stored in the sketch: S13.h
/*
    Ultrasonic Distance Sensor
    
    - Pins   VCC: +5VDC, GND: GND, Trig : Trigger (INPUT), Echo: Echo (OUTPUT)
*/

/* Initialize
=========1=========2=========3=========4=========5=========6=========7========*/
MyMessage msgS13(S13, V_DISTANCE);

/* Setup
=========1=========2=========3=========4=========5=========6=========7========*/
void setupS13(){
      //Define inputs and outputs
      pinMode(pinS13T, OUTPUT);
      pinMode(pinS13E, INPUT);
}

/* Loop
=========1=========2=========3=========4=========5=========6=========7========*/
void loopS13(){
      // The sensor is triggered by a HIGH pulse of 10 or more microseconds.
      // Give a short LOW pulse beforehand to ensure a clean HIGH pulse:
      digitalWrite(pinS13T, LOW);   delayMicroseconds(5);
      digitalWrite(pinS13T, HIGH);  delayMicroseconds(10);
      digitalWrite(pinS13T, LOW);
     
      // Read the signal from the sensor: a HIGH pulse whose duration is the time (in microseconds)
      // from the sendingof the ping to the reception of its echo off of an object.
      pinMode(pinS13E, INPUT);
      duration = pulseIn(pinS13E, HIGH);
     
      // convert the time into a distance
      cm = (duration/2) / 29.1;
      inches = (duration/2) / 74; 
      
      Serial.print(inches); Serial.print("in, "); Serial.print(cm); Serial.print("cm"); Serial.println();
      delay(250);
}

// code stored in the sketch: S14.h
/*
    Gas Detection (MQ2)
    
    - Pins  1	+5VDC
			2	GND
			3	
			4	A0
*/

/* Initialize
=========1=========2=========3=========4=========5=========6=========7========*/
MyMessage msgS14(S14, V_LEVEL);


/* Extras
=========1=========2=========3=========4=========5=========6=========7========*/

/****************** MQResistanceCalculation ****************************************
Input:   raw_adc - raw value read from adc, which represents the voltage
Output:  the calculated sensor resistance
Remarks: The sensor and the load resistor forms a voltage divider. Given the voltage
         across the load resistor and its resistance, the resistance of the sensor
         could be derived.
************************************************************************************/
float MQResistanceCalculation(int raw_adc){
    return ( ((float)RL_VALUE*(1023-raw_adc)/raw_adc));
}

/***************************** MQCalibration ****************************************
Input:   pinS14 - analog channel
Output:  Ro of the sensor
Remarks: This function assumes that the sensor is in clean air. It use
         MQResistanceCalculation to calculates the sensor resistance in clean air
         and then divides it with RO_CLEAN_AIR_FACTOR. RO_CLEAN_AIR_FACTOR is about
         10, which differs slightly between different sensors.
************************************************************************************/
float MQCalibration(int pinS14){
    int i;
    float valueS14=0;

    for (i=0; i<CALIBARAION_SAMPLE_TIMES; i++) {          //take multiple samples
        valueS14 += MQResistanceCalculation(analogRead(pinS14));
        delay(CALIBRATION_SAMPLE_INTERVAL);
    }
    valueS14 = valueS14/CALIBARAION_SAMPLE_TIMES;                   //calculate the average value

    valueS14 = valueS14/RO_CLEAN_AIR_FACTOR;                        //divided by RO_CLEAN_AIR_FACTOR yields the Ro
    //according to the chart in the datasheet

    return valueS14;
}
/*****************************  MQRead *********************************************
Input:   pinS14 - analog channel
Output:  Rs of the sensor
Remarks: This function use MQResistanceCalculation to caculate the sensor resistenc (Rs).
         The Rs changes as the sensor is in the different consentration of the target
         gas. The sample times and the time interval between samples could be configured
         by changing the definition of the macros.
************************************************************************************/
float MQRead(int pinS14){
    int i;
    float rs=0;

    for (i=0; i<READ_SAMPLE_TIMES; i++) {
        rs += MQResistanceCalculation(analogRead(pinS14));
        delay(READ_SAMPLE_INTERVAL);
    }

    rs = rs/READ_SAMPLE_TIMES;

    return rs;
}

/*****************************  MQGetPercentage **********************************
Input:   rs_ro_ratio - Rs divided by Ro
         pcurve      - pointer to the curve of the target gas
Output:  ppm of the target gas
Remarks: By using the slope and a point of the line. The x(logarithmic value of ppm)
         of the line could be derived if y(rs_ro_ratio) is provided. As it is a
         logarithmic coordinate, power of 10 is used to convert the result to non-logarithmic
         value.
************************************************************************************/
int  MQGetPercentage(float rs_ro_ratio, float *pcurve){
    return (pow(10,( ((log(rs_ro_ratio)-pcurve[1])/pcurve[2]) + pcurve[0])));
}

/*****************************  MQGetGasPercentage **********************************
Input:   rs_ro_ratio - Rs divided by Ro
         gas_id      - target gas type
Output:  ppm of the target gas
Remarks: This function passes different curves to the MQGetPercentage function which
         calculates the ppm (parts per million) of the target gas.
************************************************************************************/
int MQGetGasPercentage(float rs_ro_ratio, int gas_id){
    if ( gas_id == GAS_LPG ) {
        return MQGetPercentage(rs_ro_ratio,LPGCurve);
    } else if ( gas_id == GAS_CO ) {
        return MQGetPercentage(rs_ro_ratio,COCurve);
    } else if ( gas_id == GAS_SMOKE ) {
        return MQGetPercentage(rs_ro_ratio,SmokeCurve);
    }

    return 0;
}


/* Setup
=========1=========2=========3=========4=========5=========6=========7========*/
void setupS14(){
    Ro = MQCalibration(pinS14);
    // Calibrating the sensor. Please make sure the sensor is in clean air
	Serial.print("Calibrated to :");Serial.println(Ro);
}

/* Loop
=========1=========2=========3=========4=========5=========6=========7========*/
void loopS14(){
    uint16_t valMQ = MQGetGasPercentage(MQRead(pinS14)/Ro,GAS_CO);
    Serial.print("Raw:");Serial.println(valueS14);

    Serial.print("LPG:");
    Serial.print(MQGetGasPercentage(MQRead(pinS14)/Ro,GAS_LPG) );
    Serial.print( "ppm" );
    Serial.print("    ");
    Serial.print("CO:");
    Serial.print(MQGetGasPercentage(MQRead(pinS14)/Ro,GAS_CO) );
    Serial.print( "ppm" );
    Serial.print("    ");
    Serial.print("SMOKE:");
    Serial.print(MQGetGasPercentage(MQRead(pinS14)/Ro,GAS_SMOKE) );
    Serial.print( "ppm" );
    Serial.print("\n");

    if (valMQ != lastMQ) {
        send(msgS14.set((int16_t)ceil(valMQ)));
        lastMQ = ceil(valMQ);
    }
}

// code stored in the sketch: s2.h
/*
    PhotoVoltaic Sensor

=========1=========2=========3=========4=========5=========6=========7========*/
MyMessage msg_s2(2, V_LIGHT_LEVEL);    // define type of message sent to MySensors

/* Setup
=========1=========2=========3=========4=========5=========6=========7========*/
void setup_s2(){
    pinMode(pvPin, INPUT);             // initialize sensor as an input
}

/* Loop
=========1=========2=========3=========4=========5=========6=========7========*/
void loop_s2(){
    pvVal = analogRead(pvPin);   	   // read and store sensor value
    Serial.print("Light is at: "); Serial.println(pvVal);
    if (pvState != pvVal){             // if the state has changed
        pvState = pvVal;               // update state
        //  send message to mycontroller
        send(msg_s2.set(pvVal));
    }
}

/*
    // a few threshholds, qualitatively determined
    if (pvVal < 10) {
        Serial.println(" - Dark");
    } else if (pvVal < 200) {
        Serial.println(" - Dim");
    } else if (pvVal < 500) {
        Serial.println(" - Light");
    } else if (pvVal < 800) {
        Serial.println(" - Bright");
    } else {
        Serial.println(" - Very bright");
    }
 */

// code stored in the sketch: s3.h
/* Single Relay actuator
=========1=========2=========3=========4=========5=========6=========7========*/
const int relayPin = 3;                 // define switch pin
MyMessage msgRel(3, V_STATUS);          // define type of message sent to MySensors

/* Setup
=========1=========2=========3=========4=========5=========6=========7========*/
void setup_s3(){
    pinMode(3, OUTPUT);                     // set pin 3 in output mode
    /*digitalWrite(relayPin, loadState(3) ? 1 : 0);  // Set relay to last known state (using eeprom storage) */
}

/* Receive
=========1=========2=========3=========4=========5=========6=========7========*/
void receive_s3(const MyMessage &message){
    if (message.type==V_LIGHT) {                           // We only expect one type of message from controller.
        digitalWrite(relayPin, message.getBool() ? 1 : 0);  // Toggle relay state
        /*saveState(3, message.getBool());                // Store state in eeprom*/
        // Serial.print("Toggle relay. New state is "); Serial.println(message.getBool());
   } 
}

// code stored in the sketch: S4.h
/* 
    Passive InfraRed Switch
*/

/* Initialize
=========1=========2=========3=========4=========5=========6=========7========*/
MyMessage msgS4(S4, V_TRIPPED);        // type of message sent to MySensors

/* Setup
=========1=========2=========3=========4=========5=========6=========7========*/
void setupS4(){
    pinMode(pinS4, INPUT);             // initialize sensor as an input
	stateS4 = request(S4, V_TRIPPED);  // get status from controller
    digitalWrite(pinS4, stateS4);      // turn on/off based on controller state

}

/* Loop
=========1=========2=========3=========4=========5=========6=========7========*/
void loopS4(){
    valueS4 = digitalRead(pinS4);     	// read sensor value
    if (valueS4 == 1 && stateS4 == 0){	
        stateS4 = 1;                  	// update state to HIGH
        tS4 = millis();					// time when loop fired (for calibrating the timer)
        Serial.println("--- Motion detected! --- ");
    } else if (valueS4 == 0 && stateS4 == 1){
        stateS4 = 0;                    // update state to LOW
        Serial.print("- Standing down after "); Serial.println((millis()-tS4)/1000);
    }
    send(msgS4.set(valueS4));           // Send value to gw
    wait(5000);							// wait 5 seconds so it doesnt bounce
}

// code stored in the sketch: xxx.h
/*
    FRONT DOOR

    RADIO
repeater

    SENSORS
PIR switch - to check if someone is in front of the door
Reed switch - to sense if door is open or closed
Photovoltaic sensor -  to check if it's day or night
? Electric lock - status if door is locked

    ACTUATORS
Relay, to switch on the lights
? Lock/Unlock via electrick lock

*/

// code stored in the sketch: zzz.h
/*  
				FRONT DOOR
*/
//
//  SENSORS
//
/*=======1=========2=========3=========4=========5=========6=========7========*/
//
//  s0    PIR switch - to check if someone is in front of the door
//
const int pirPin = 2;                  // the pin that the PIR motion detector is atteched to
int pirState = LOW;                    // by default, no motion is detected
int pirVal = 0;                        // variable to store the PIR value
int pirTimer =0;                       // variable to store the number of loops
//
//  s1  Reed switch - to sense if the door is open or closed
//
const int reedPin = 3;                 // the pin that the reed switch is atteched to
int reedVal = 0;                       // variable to store the reed switch last state
//
//  s2  Photovoltaic sensor -  to check if it's day or night
//
const int pvPin = A0;                  // the pin that the photovoltaic sensor is attached to
int pvState = 0;                       // default state, dark
int pvVal = 0;                         // variable to store photovoltaic sensor value
//
//  ACTUATORS
//
/*=======1=========2=========3=========4=========5=========6=========7========*/
//
//  a0  Relay, to switch on the lights if it's dark and motion is detected
//
const int relayPin = 5;                 // the pin that the relay is atteched to
int relayState = 0;                     // by default, the relay is off
//
//  a1 Lock/Unlock via electrick lock  ???
//
const int lockPin = 6;                  // the pin that the door relay is atteched to
int lockState = 0;                      // by default, the door is locked
