# Fritzing sketch node12_Workshop (saved by Fritzing 0.9.3b)
circuit board: 6cm x 4cm
perfboards: 2

parts:
  HLK-PM1 = HLK-PM01
  Part5 = Arduino Nano (Rev3.0)
  U2 = SWITCH-SPST-2 [package=switch-spst-vertical]
  Part6 = NRF24L01+ Breakout Board
  Power_plug1 = Power plug
  JP1 = Header 6 [package=1x06_smd_straight_alt]  # not connected
  Part7 = ACS712 Low Current Sensor Board v12
  R1 = Resistor [tolerance=±5% resistance=10k package=THT]
  R2 = Resistor [tolerance=±5% resistance=1k package=THT]
  VCC1 = Battery block 9V

nets:
  N1: HLK-PM1.AC#0, U2.P
  N2: HLK-PM1.AC#1, Power_plug1.GND
  GND: Part5.GND, Part6.GND
  N3: Part5.D9, Part6.CE
  N4: Part5.D10, Part6.CS
  N5: Part5.D11/MOSI, Part6.MOSI
  N6: Part5.D12/MISO, Part6.MISO
  N7: Part5.A2, R1.Pin_1, R2.Pin_0
  N8: Part5.A1, Part7.VO
  3V3: Part5.3V3, Part6.VCC
  N9: Part5.D13/SCK, Part6.SCK
  N10: U2.O, Power_plug1.VCC
  N11: Part7.IP+, R1.Pin_0, VCC1.+
  N12: Part7.IP-, VCC1.-

// code stored in the sketch: _1_FrontDoor.ino

#define SN "Front Door"                 // short Sketch name
#define SV "0.9"                        // short Sketch version
#define MY_NODE_ID 1                    // (1-254) to manually set Node ID

/* Includes
=========1=========2=========3=========4=========5=========6=========7========*/
#include "NRF24L01.h"                   // NRF24L01 definitions
#include <MySensors.h>                  // MySensors library
#include "zzz.h"                        // Explanation and inital variables

//#include "a0.h"                         // Relay, to switch on the lights when needed
//#include "a1.h"                         // Lock and unlock the front door

#include "s0.h"                         // PIR switch, check if someone is in front of the door
#include "s1.h"                         // Reed switch, check if door is open or closed
#include "s2.h"                         // Photovoltaic sensor, to check if it's dark

/* Presentation
=========1=========2=========3=========4=========5=========6=========7========*/
void presentation(){ 
    sendSketchInfo(SN, SV);             // Send the sketch version information
    // Register the sensor(s) to the controller
    /* void present(uint8_t childSensorId, uint8_t sensorType, const char *description, bool ack); */
    present(0, S_MOTION, "PIR switch");
    present(1, S_DOOR, "Reed switch");
    present(2, S_LIGHT_LEVEL, "PV switch");
//    present(3, S_BINARY, "Lights relay");
    //Serial.println("=== Node presented === ");
}

/* Setup
=========1=========2=========3=========4=========5=========6=========7========*/
void setup() {
    setup_s0();
    setup_s1();
    setup_s2();
//    setup_a0();
    //Serial.println( "=== Node setup done ===" );
}

/* Loop
=========1=========2=========3=========4=========5=========6=========7========*/
void loop() {
    loop_s0();
    loop_s1();
    loop_s2();
    wait(2000);                         // wait a bit, loop once every 2 seconds
}

/* Receive
=========1=========2=========3=========4=========5=========6=========7========*/
/*void receive(const MyMessage &message) {
//    receive_a0(message);
    //Serial.println("=== Node message received === ");
}*/

// code stored in the sketch: _3_Patio.ino
#define SN "Patio"                      // short Sketch (Node) name
#define SV "1.1"                        // short Sketch (Node) version
#define MY_NODE_ID 1                    // (1-254) to manually set Node ID

/* Includes
=========1=========2=========3=========4=========5=========6=========7========*/
#include "NRF24L01.h"                   // NRF24L01 definitions
#include <MySensors.h>                  // MySensors library
#include "s1.h"                         // DHT11 for Temperature and Humidity
#include "a1.h"                         // Relay for Spotlight

/* Presentation
=========1=========2=========3=========4=========5=========6=========7========*/
void presentation(){ 
    sendSketchInfo(SN, SV);             // Send the sketch version information
    // Register sensor(s) to gateway    // void present(uint8_t childSensorId, uint8_t sensorType, const char *description, bool ack);
    present(0, S_HUM,"Patio Humidity");             // present sensor to gateway
    present(1, S_TEMP,"Patio Temperature");         // present sensor to gateway
    present(2, S_BINARY,"Patio Spotlight");         // present sensor to gateway
    metric = getConfig().isMetric;                  // ???
    //Serial.println("=== Node presented === ");    // Debug
}

/* Setup
=========1=========2=========3=========4=========5=========6=========7========*/
void setup(){
    setup_a1();
    setup_s1();
    //Serial.println( "=== Node setup done ===" ); // Debug
}

/* Loop
=========1=========2=========3=========4=========5=========6=========7========*/
void loop(){
    loop_s1();
}

/* Receive
=========1=========2=========3=========4=========5=========6=========7========*/
void receive(const MyMessage &message) {
    receive_a1(message);
    //Serial.println("=== Node message received === "); // Debug
}

// code stored in the sketch: a0.h
/*
    Single Relay actuator for door lights

=========1=========2=========3=========4=========5=========6=========7========*/
MyMessage msg_a0(3, V_STATUS);          // define type of message sent to MySensors

/* Setup
=========1=========2=========3=========4=========5=========6=========7========*/
void setup_a0(){
    pinMode(relayPin, OUTPUT);         // set pin to output mode
}

/* Receive
=========1=========2=========3=========4=========5=========6=========7========*/
void receive_a0(const MyMessage &message){
    if (message.type==V_LIGHT) {       // We only expect one type of message from controller.
        digitalWrite(relayPin, message.getBool() ? 1 : 0);  // Toggle relay state
        // Serial.print("Toggle relay. New state is "); Serial.println(message.getBool());
   } 
}

/* ON
=========1=========2=========3=========4=========5=========6=========7========*/
void lightsOn(){
    if (pvState < 500) {               // only switch on if PV sensor says it's dark
        digitalWrite(relayPin, 1);     // switch off 
    }
}

/* OFF
=========1=========2=========3=========4=========5=========6=========7========*/
void lightsOff(int t){
    wait(t * 60 * 1000);               // wait for t minutes
    digitalWrite(relayPin, 0);         // then switch off 
}

// code stored in the sketch: a0.h.ino
/* Single Relay actuator
=========1=========2=========3=========4=========5=========6=========7========*/
const int relayPin = 3;                 // define switch pin
MyMessage msgRel(3, V_STATUS);          // define type of message sent to MySensors

/* Setup
=========1=========2=========3=========4=========5=========6=========7========*/
void setup_s3(){
    pinMode(3, OUTPUT);                     // set pin 3 in output mode
    /*digitalWrite(relayPin, loadState(3) ? 1 : 0);  // Set relay to last known state (using eeprom storage) */
}

/* Receive
=========1=========2=========3=========4=========5=========6=========7========*/
void receive_s3(const MyMessage &message){
    if (message.type==V_LIGHT) {                           // We only expect one type of message from controller.
        digitalWrite(relayPin, message.getBool() ? 1 : 0);  // Toggle relay state
        /*saveState(3, message.getBool());                // Store state in eeprom*/
        // Serial.print("Toggle relay. New state is "); Serial.println(message.getBool());
   } 
}

// code stored in the sketch: a1.h
/* Single Relay actuator
=========1=========2=========3=========4=========5=========6=========7========*/
MyMessage msgRel(2, V_LIGHT);
#define relayPin  3                     // Digital pin number for the relay
#define RELAY_ON 1                      // GPIO value to write to turn on attached relay
#define RELAY_OFF 0                     // GPIO value to write to turn off attached relay

/* Setup
=========1=========2=========3=========4=========5=========6=========7========*/
void setup_a1(){
    pinMode(relayPin, OUTPUT);                              // set relay pin in output mode
    digitalWrite(3, loadState(3) ? RELAY_ON : RELAY_OFF);   // Set relay to last known state (using eeprom storage) 
}

/* Receive
=========1=========2=========3=========4=========5=========6=========7========*/
void receive_a1(const MyMessage &message){
    // We only expect one type of message from controller. But we better check anyway.
    if (message.type==V_LIGHT) {
        // Change relay state
        digitalWrite(3, message.getBool() ? RELAY_ON : RELAY_OFF);
        // Store state in eeprom
        saveState(3, message.getBool());
        // Write some debug info
        Serial.print("Incoming change for relay:"); Serial.print(3);
        Serial.print(", New state: "); Serial.println(message.getBool());
   } 
}

// code stored in the sketch: A1_2.h
/*
    Multi Relay (2 channels)
*/

/* Initialize
=========1=========2=========3=========4=========5=========6=========7========*/
MyMessage msgA12A( A12A, V_STATUS );
MyMessage msgA12B( A12B, V_STATUS );

/* Setup
=========1=========2=========3=========4=========5=========6=========7========*/
void setupA1_2(){
    pinMode(pinA12A, OUTPUT);           // set relay pin in output mode
    digitalWrite(pinA12A, loadState(A12A) ? 0 : 1); // load state from eeprom
	
    pinMode(pinA12B, OUTPUT);           // set relay pin in output mode
    digitalWrite(pinA12B, loadState(A12B) ? 0 : 1); // load state from eeprom
}
/*
    Receive
=========1=========2=========3=========4=========5=========6=========7========*/
void receiveA1_2(const MyMessage &message){
    if (message.type == V_STATUS) {
        if (message.sensor == A12A){
            digitalWrite(pinA12A, message.getBool() ? 0 : 1);   // Toggle relay state
			saveState(A12A,message.getBool());					// save state to eeprom
            Serial.print("Toggle - New state of A12A is "); Serial.println(message.getBool());
        }
        if (message.sensor == A12B){
            digitalWrite(pinA12B, message.getBool() ? 0 : 1);   // Toggle relay state
			saveState(A12B,message.getBool());					// save state to eeprom
            Serial.print("Toggle - New state of A12B is "); Serial.println(message.getBool());
        }
   } 
}

// code stored in the sketch: def.h

/*      SENSORS
=========1=========2=========3=========4=========5=========6=========7========*/
#define A12A            1               // Relay for pump
#define A12B            2               // Relay for lights
#define S4              3               // PIR
#define S6              4               // VAC sensor


/*  PINS & VARIABLES
=========1=========2=========3=========4=========5=========6=========7========*/

// A12 - 2 Channel Relay
// ---------------------
const int pinA12A =     2;             // Relay - for shutting off pump at night
const int pinA12B =     3;             // Relay - for activating lights on PIR


/*  PINS & VARIABLES
=========1=========2=========3=========4=========5=========6=========7========*/

// S4 - PIR switch
// ---------------
const int pinS4 =       4;              // data pin
int valueS4 = 0;                        // reading the sensor status
int stateS4 = 0;                        // storing the last state
unsigned long tS4;                      // store time of last trigger
int iS4 = 0;                            // counter
unsigned long startS4;

// S6 - AC Voltage sensor
// ----------------------
const int pinS6 =       A1;             // data pin
int valueS6 = 0;                        // reading the sensor status
int stateS6 = 0;                        // storing the last state
int mVperAmp = 185; // use 185 for 5A, 100 for 20A Module and 66 for 30A Module

// code stored in the sketch: node05_Waterpump.ino
#define SN "Water Pump"                 // short Sketch (Node) name
#define SV "1.1"                        // short Sketch (Node) version
#define MY_NODE_ID 5                    // (1-254) to manually set Node ID
/*
    Includes
=========1=========2=========3=========4=========5=========6=========7========*/
#include "R.h"                          // NRF24L01 definitions
#include <MySensors.h>                  // MySensors library
#include "def.h"                        // Explanation and inital variables
  #include "A1_2.h"                     // Double relay
  #include "S4.h"                       // PIR
  #include "S6.h"                       // VAC sensor
/*
    Presentation
=========1=========2=========3=========4=========5=========6=========7========*/
void presentation(){ 
  sendSketchInfo(SN, SV);
    present(A12A, S_BINARY, "Water Pump");
    present(A12B, S_BINARY, "Water Pump Lights");
    present(S4, S_MOTION, "Water Pump PIR");
    present(S6, S_POWER, "Water Pump VAC");
  Serial.println((String)" === Node "+MY_NODE_ID+" presented ("+SN+")");
}
/*
    Setup
=========1=========2=========3=========4=========5=========6=========7========*/
void setup(){
    setupA1_2();
    setupS4();
    setupS6();
  Serial.println((String)" === Node "+MY_NODE_ID+" setup ("+SN+")");
}
/*
    Loop
=========1=========2=========3=========4=========5=========6=========7========*/
void loop(){
    loopS4();
    loopS6();
  wait(1000);
}
/*
    Receive
=========1=========2=========3=========4=========5=========6=========7========*/
void receive(const MyMessage &message) {
    receiveA1_2(message);
}

// code stored in the sketch: s0.h
/* 
    Passive InfraRed Switch

=========1=========2=========3=========4=========5=========6=========7========*/
MyMessage msg_s0(0, V_TRIPPED);        // define type of message sent to MySensors

/* Setup
=========1=========2=========3=========4=========5=========6=========7========*/
void setup_s0(){
    pinMode(pirPin, INPUT);            // initialize sensor as an input
}

/* Loop
=========1=========2=========3=========4=========5=========6=========7========*/
void loop_s0(){
    pirVal = digitalRead(pirPin);               // read and store sensor value
    //Serial.print("PIR is at: "); Serial.println(pirVal);
    if (pirVal == HIGH && pirState == LOW) {    // check if the sensor is tripped
        Serial.println("-----> Motion detected!");
        pirState = HIGH;       	                // update variable state to HIGH
        pirTimer ++;
//        lightsOn();                           // Switch on lights
    }
    if (pirState == HIGH && pirTimer>60){
        pirState = LOW;                           // update variable state to LOW
        pirTimer=0;
//        lightsOff(5);                         // Set timer to switch off light 5 minutes
    }
    send(msg_s0.set(pirVal ? "1" : "0"));       // Send tripped value to gw
}

// code stored in the sketch: s1.h
/*
    Reed Switch

=========1=========2=========3=========4=========5=========6=========7========*/
MyMessage msg_s1(1, V_TRIPPED);        // define type of message sent to MySensors

/* Setup
=========1=========2=========3=========4=========5=========6=========7========*/
void setup_s1(){
    pinMode(reedPin, INPUT);           // initialize sensor as an input
}

/* Loop
=========1=========2=========3=========4=========5=========6=========7========*/
void loop_s1(){
    reedVal = digitalRead(reedPin);   	 // read and store sensor value
    //Serial.print("Reed is at: "); Serial.println(reedVal);
    if (reedVal == HIGH) {        // check if the sensor is tripped
        Serial.println("Your Door is Closed");
    } else {
        Serial.println("Your Door is Open");
    }
    send(msg_s1.set(reedVal ? "0" : "1"));       // Send tripped value to gw
}

// code stored in the sketch: s2.h
/*
    PhotoVoltaic Sensor

=========1=========2=========3=========4=========5=========6=========7========*/
MyMessage msg_s2(2, V_LIGHT_LEVEL);    // define type of message sent to MySensors

/* Setup
=========1=========2=========3=========4=========5=========6=========7========*/
void setup_s2(){
    pinMode(pvPin, INPUT);             // initialize sensor as an input
}

/* Loop
=========1=========2=========3=========4=========5=========6=========7========*/
void loop_s2(){
    pvVal = analogRead(pvPin);   	   // read and store sensor value
    Serial.print("Light is at: "); Serial.println(pvVal);
    if (pvState != pvVal){             // if the state has changed
        pvState = pvVal;               // update state
        //  send message to mycontroller
        send(msg_s2.set(pvVal));
    }
}

/*
    // a few threshholds, qualitatively determined
    if (pvVal < 10) {
        Serial.println(" - Dark");
    } else if (pvVal < 200) {
        Serial.println(" - Dim");
    } else if (pvVal < 500) {
        Serial.println(" - Light");
    } else if (pvVal < 800) {
        Serial.println(" - Bright");
    } else {
        Serial.println(" - Very bright");
    }
 */

// code stored in the sketch: s3.h
/* Single Relay actuator
=========1=========2=========3=========4=========5=========6=========7========*/
const int relayPin = 3;                 // define switch pin
MyMessage msgRel(3, V_STATUS);          // define type of message sent to MySensors

/* Setup
=========1=========2=========3=========4=========5=========6=========7========*/
void setup_s3(){
    pinMode(3, OUTPUT);                     // set pin 3 in output mode
    /*digitalWrite(relayPin, loadState(3) ? 1 : 0);  // Set relay to last known state (using eeprom storage) */
}

/* Receive
=========1=========2=========3=========4=========5=========6=========7========*/
void receive_s3(const MyMessage &message){
    if (message.type==V_LIGHT) {                           // We only expect one type of message from controller.
        digitalWrite(relayPin, message.getBool() ? 1 : 0);  // Toggle relay state
        /*saveState(3, message.getBool());                // Store state in eeprom*/
        // Serial.print("Toggle relay. New state is "); Serial.println(message.getBool());
   } 
}

// code stored in the sketch: S4.h
/* 
    Passive InfraRed Switch
	
*/

/* Initialize
=========1=========2=========3=========4=========5=========6=========7========*/
MyMessage msgS4(S4, V_TRIPPED);        // type of message sent to MySensors

/* Setup
=========1=========2=========3=========4=========5=========6=========7========*/
void setupS4(){
    pinMode(pinS4, INPUT);             // initialize sensor as an input
	stateS4 = request(S4, V_TRIPPED);  // get status from controller
    digitalWrite(pinS4, stateS4);      // turn on/off based on controller state

}

/* Loop
=========1=========2=========3=========4=========5=========6=========7========*/
void loopS4(){
	valueS4 = digitalRead(pinS4);       // Read the state of the switch
	if (valueS4 != stateS4) {           // If different from last state
        if (valueS4 == 0){              // Pin reads low, the door is closed.
			Serial.println((String)"- Standing down after "+ ((millis()-tS4)/1000) + " seconds");
        } else if (valueS4 == 1){
			tS4 = millis();				// time when loop fired (for calibrating the timer)
			Serial.println("--- Motion detected! --- ");
        }
        send(msgS4.set(valueS4));       // send to controller
        stateS4 = valueS4;              // update state
		wait(2000);						// wait 2 seconds so it doesnt bounce
    }
}

// code stored in the sketch: S6.h
/*
    VAC Sensor (ACS712)
	

*/

/* Initialize    
=========1=========2=========3=========4=========5=========6=========7========*/
MyMessage msgS6W(S6, V_WATT);


/* Setup
=========1=========2=========3=========4=========5=========6=========7========*/
void setupS6(){
    pinMode(pinS6, INPUT);
	stateS6 = analogRead(pinS6);
}


/* Loop
=========1=========2=========3=========4=========5=========6=========7========*/
void loopS6(){
	valueS6 = analogRead(pinS6);
	float Voltage = (valueS6 * 5.0 / 1024.0);					// 5 volts, 1024 values, should give 2.5v at no current
	float Amps = abs((Voltage - 2.5) * 1000 / mVperAmp);		// absolute value
	float Watts = 1 * Amps * 117.0;								// W = PF × A × V

	// printout
	//Serial.print("   V:"); Serial.print(Voltage);
	//Serial.print("  A:"); if(Amps>=0){Serial.print(" ");} Serial.print(Amps);
	//Serial.print("  W:"); if(Watts>=0){Serial.print(" ");} Serial.println(Watts);
	
	// send to mycontroller (only if changed significantly ?? )
	if ( Watts<40 ) {
		send(msgS6W.set(0));
	}
	else {
		send(msgS6W.set(Watts,2));
	}
}

// code stored in the sketch: xxx.h
/*
    FRONT DOOR

    RADIO
repeater

    SENSORS
PIR switch - to check if someone is in front of the door
Reed switch - to sense if door is open or closed
Photovoltaic sensor -  to check if it's day or night
? Electric lock - status if door is locked

    ACTUATORS
Relay, to switch on the lights
? Lock/Unlock via electrick lock

*/

// code stored in the sketch: zzz.h
/*  
				FRONT DOOR
*/
//
//  SENSORS
//
/*=======1=========2=========3=========4=========5=========6=========7========*/
//
//  s0    PIR switch - to check if someone is in front of the door
//
const int pirPin = 2;                  // the pin that the PIR motion detector is atteched to
int pirState = LOW;                    // by default, no motion is detected
int pirVal = 0;                        // variable to store the PIR value
int pirTimer =0;                       // variable to store the number of loops
//
//  s1  Reed switch - to sense if the door is open or closed
//
const int reedPin = 3;                 // the pin that the reed switch is atteched to
int reedVal = 0;                       // variable to store the reed switch last state
//
//  s2  Photovoltaic sensor -  to check if it's day or night
//
const int pvPin = A0;                  // the pin that the photovoltaic sensor is attached to
int pvState = 0;                       // default state, dark
int pvVal = 0;                         // variable to store photovoltaic sensor value
//
//  ACTUATORS
//
/*=======1=========2=========3=========4=========5=========6=========7========*/
//
//  a0  Relay, to switch on the lights if it's dark and motion is detected
//
const int relayPin = 5;                 // the pin that the relay is atteched to
int relayState = 0;                     // by default, the relay is off
//
//  a1 Lock/Unlock via electrick lock  ???
//
const int lockPin = 6;                  // the pin that the door relay is atteched to
int lockState = 0;                      // by default, the door is locked
